// Logisim project Circuitos.circ as structural Verilog
module Somador_Completo (
  input  A,
  input  B,
  input  Vem1,
  output Soma,
  output Vai1
);

  wire and_1_out, and_2_out, and_3_out, xor_1_out;

  xor xor_1 (xor_1_out, A, B);
  and and_1 (and_1_out, A, B);
  and and_2 (and_2_out, Vem1, A);
  and and_3 (and_3_out, Vem1, B);
  xor xor_2 (Soma, xor_1_out, Vem1);
  or or_1 (Vai1, and_1_out, and_2_out, and_3_out);
endmodule

module Multiplexador_2x1 (
  input  A,
  input  B,
  input  Sel,
  output S
);

  wire and_1_out, and_2_out, not_1_out;

  not not_1 (not_1_out, Sel);
  and and_1 (and_1_out, A, not_1_out);
  and and_2 (and_2_out, B, Sel);
  or or_1 (S, and_1_out, and_2_out);
endmodule

module Multiplexador_4x1 (
  input  _00,
  input  _1,
  input  _2,
  input  _3,
  input  Sel0,
  input  Sel1,
  output out_7
);

  wire multiplexador_2x1_1_s, multiplexador_2x1_2_s;

  Multiplexador_2x1 multiplexador_2x1_1 (.A(_00), .B(_1), .Sel(Sel1), .S(multiplexador_2x1_1_s));
  Multiplexador_2x1 multiplexador_2x1_2 (.A(_2), .B(_3), .Sel(Sel1), .S(multiplexador_2x1_2_s));
  Multiplexador_2x1 multiplexador_2x1_3 (.A(multiplexador_2x1_1_s), .B(multiplexador_2x1_2_s), .Sel(Sel0), .S(out_7));
endmodule

module Multiplexador_8x1 (
  input  _0,
  input  _1,
  input  _2,
  input  _3,
  input  _4,
  input  _5,
  input  _6,
  input  _7,
  input  Sel0,
  input  Sel1,
  input  Sel2,
  output out_12
);

  wire multiplexador_4x1_1_out_7, multiplexador_4x1_2_out_7;

  Multiplexador_4x1 multiplexador_4x1_1 (
    ._00(_0), ._1(_1), ._2(_2), ._3(_3), .Sel0(Sel1), .Sel1(Sel2), .out_7(multiplexador_4x1_1_out_7));
  Multiplexador_4x1 multiplexador_4x1_2 (
    ._00(_4), ._1(_5), ._2(_6), ._3(_7), .Sel0(Sel1), .Sel1(Sel2), .out_7(multiplexador_4x1_2_out_7));
  Multiplexador_2x1 multiplexador_2x1_1 (
    .A(multiplexador_4x1_1_out_7), .B(multiplexador_4x1_2_out_7), .Sel(Sel0), .S(out_12));
endmodule

module Multiplexador_16x1 (
  input  in_1,
  input  in_2,
  input  in_3,
  input  in_4,
  input  in_5,
  input  in_6,
  input  in_7,
  input  in_8,
  input  in_9,
  input  in_10,
  input  in_11,
  input  in_12,
  input  in_13,
  input  in_14,
  input  in_15,
  input  in_16,
  input  Sel0,
  input  Sel0_2,
  input  Sel0_3,
  input  Sel3,
  output out_21
);

  wire multiplexador_8x1_1_out_12, multiplexador_8x1_2_out_12;

  Multiplexador_8x1 multiplexador_8x1_1 (
    ._0(in_1), ._1(in_2), ._2(in_3), ._3(in_4), ._4(in_5), ._5(in_6), ._6(in_7), ._7(in_8), .Sel0(Sel0_2),
    .Sel1(Sel0_3), .Sel2(Sel3), .out_12(multiplexador_8x1_1_out_12));
  Multiplexador_8x1 multiplexador_8x1_2 (
    ._0(in_9), ._1(in_10), ._2(in_11), ._3(in_12), ._4(in_13), ._5(in_14), ._6(in_15), ._7(in_16),
    .Sel0(Sel0_2), .Sel1(Sel0_3), .Sel2(Sel3), .out_12(multiplexador_8x1_2_out_12));
  Multiplexador_2x1 multiplexador_2x1_1 (
    .A(multiplexador_8x1_1_out_12), .B(multiplexador_8x1_2_out_12), .Sel(Sel0), .S(out_21));
endmodule

module Multiplexador_32x1 (
  input  _0,
  input  _1,
  input  _2,
  input  _3,
  input  _4,
  input  _5,
  input  _6,
  input  _7,
  input  _8,
  input  _9,
  input  _10,
  input  _11,
  input  _12,
  input  _13,
  input  _14,
  input  _15,
  input  _16,
  input  _17,
  input  _18,
  input  _19,
  input  _20,
  input  _21,
  input  _22,
  input  _23,
  input  _24,
  input  _25,
  input  _26,
  input  _27,
  input  _28,
  input  _29,
  input  _30,
  input  _31,
  input  Sel0,
  input  Sel1,
  input  Sel2,
  input  Sel3,
  input  Sel4,
  output out_38
);

  wire multiplexador_16x1_1_out_21, multiplexador_16x1_2_out_21;

  Multiplexador_16x1 multiplexador_16x1_1 (
    .in_1(_0), .in_2(_1), .in_3(_2), .in_4(_3), .in_5(_4), .in_6(_5), .in_7(_6), .in_8(_7), .in_9(_8),
    .in_10(_9), .in_11(_10), .in_12(_11), .in_13(_12), .in_14(_13), .in_15(_14), .in_16(_15), .Sel0(Sel1),
    .Sel0_2(Sel2), .Sel0_3(Sel3), .Sel3(Sel4), .out_21(multiplexador_16x1_1_out_21));
  Multiplexador_16x1 multiplexador_16x1_2 (
    .in_1(_16), .in_2(_17), .in_3(_18), .in_4(_19), .in_5(_20), .in_6(_21), .in_7(_22), .in_8(_23),
    .in_9(_24), .in_10(_25), .in_11(_26), .in_12(_27), .in_13(_28), .in_14(_29), .in_15(_30), .in_16(_31),
    .Sel0(Sel1), .Sel0_2(Sel2), .Sel0_3(Sel3), .Sel3(Sel4), .out_21(multiplexador_16x1_2_out_21));
  Multiplexador_2x1 multiplexador_2x1_1 (
    .A(multiplexador_16x1_1_out_21), .B(multiplexador_16x1_2_out_21), .Sel(Sel0), .S(out_38));
endmodule

module \Detector_Subtração  (
  input  [4:0] in_1,
  output Sub
);

  and and_1 (Sub, ~in_1[0], ~in_1[1], in_1[2], ~in_1[3], ~in_1[4]);  // AND_Gate
endmodule

module \Célula_ULA  (
  input  Vem1,
  input  A,
  input  B,
  input  [4:0] \Opção ,
  output Resultado,
  output Vai1
);

  wire and_1_out, detector_slt_1_out_2, \detector_subtração_1_sub , multiplexador_2x1_1_s, nor_1_out,
       not_1_out, or_1_out, or_2_out, somador_completo_1_soma, xor_1_out;

  not not_1 (not_1_out, B);
  Multiplexador_2x1 multiplexador_2x1_1 (.A(B), .B(not_1_out), .Sel(or_1_out), .S(multiplexador_2x1_1_s));
  Somador_Completo somador_completo_1 (
    .A(A), .B(multiplexador_2x1_1_s), .Vem1(Vem1), .Soma(somador_completo_1_soma), .Vai1(Vai1));
  or or_1 (or_1_out, detector_slt_1_out_2, \detector_subtração_1_sub );
  and and_1 (and_1_out, A, B);
  or or_2 (or_2_out, A, B);
  xor xor_1 (xor_1_out, A, B);
  nor nor_1 (nor_1_out, A, B);
  Detector__SLT detector_slt_1 (.in_1(\Opção ), .out_2(detector_slt_1_out_2));
  \Detector_Subtração  \detector_subtração_1  (.Sub(\detector_subtração_1_sub ), .in_1(\Opção ));
  Multiplexador_32x1 multiplexador_32x1_1 (
    ._0(and_1_out), ._1(or_2_out), ._2(xor_1_out), ._3(somador_completo_1_soma),
    ._4(somador_completo_1_soma), ._5(nor_1_out), ._6(somador_completo_1_soma), ._7(somador_completo_1_soma),
    ._8(somador_completo_1_soma), ._9(somador_completo_1_soma), ._10(somador_completo_1_soma),
    ._11(somador_completo_1_soma), ._12(somador_completo_1_soma), ._13(somador_completo_1_soma),
    ._14(somador_completo_1_soma), ._15(somador_completo_1_soma), ._16(somador_completo_1_soma),
    ._17(somador_completo_1_soma), ._18(somador_completo_1_soma), ._19(somador_completo_1_soma),
    ._20(somador_completo_1_soma), ._21(somador_completo_1_soma), ._22(somador_completo_1_soma),
    ._23(somador_completo_1_soma), ._24(somador_completo_1_soma), ._25(somador_completo_1_soma),
    ._26(somador_completo_1_soma), ._27(somador_completo_1_soma), ._28(somador_completo_1_soma),
    ._29(somador_completo_1_soma), ._30(somador_completo_1_soma), ._31(somador_completo_1_soma),
    .Sel0(\Opção [4]), .Sel1(\Opção [3]), .Sel2(\Opção [2]), .Sel3(\Opção [1]), .Sel4(\Opção [0]),
    .out_38(Resultado));
endmodule

module ULA_32bits (
  input  [31:0] A,
  input  [31:0] B,
  input  [4:0] \Opção ,
  output out_4,
  output OverFlowNat,
  output [31:0] Resultado
);

  wire \célula_ula_2_vai1 , \célula_ula_3_vai1 , \célula_ula_4_vai1 , \célula_ula_5_vai1 ,
       \célula_ula_6_vai1 , \célula_ula_7_vai1 , \célula_ula_8_vai1 , \célula_ula_9_vai1 ,
       \célula_ula_10_vai1 , \célula_ula_11_vai1 , \célula_ula_12_vai1 , \célula_ula_13_vai1 ,
       \célula_ula_14_vai1 , \célula_ula_15_vai1 , \célula_ula_16_vai1 , \célula_ula_17_vai1 ,
       \célula_ula_18_vai1 , \célula_ula_19_vai1 , \célula_ula_20_vai1 , \célula_ula_21_vai1 ,
       \célula_ula_22_vai1 , \célula_ula_23_vai1 , \célula_ula_24_vai1 , \célula_ula_25_vai1 ,
       \célula_ula_26_vai1 , \célula_ula_27_vai1 , \célula_ula_28_vai1 , \célula_ula_29_vai1 ,
       \célula_ula_30_vai1 , \célula_ula_31_vai1 , \célula_ula_32_vai1 , detector_slt_1_out_2,
       \detector_subtração_1_sub , Mux_s, or_1_out;
  wire [31:0] \célula_ula_32_resultado ;

  OverFlowInt overflowint_1 (.in_1(\célula_ula_32_resultado [31]), .in_2(B[31]), .in_3(A[31]), .out_4(out_4));
  \Célula_ULA  \célula_ula_1  (
    .Vai1(OverFlowNat), .A(A[31]), .B(B[31]), .\Opção (\Opção ), .Vem1(\célula_ula_2_vai1 ),
    .Resultado(\célula_ula_32_resultado [31]));
  \Célula_ULA  \célula_ula_2  (
    .Vai1(\célula_ula_2_vai1 ), .A(A[30]), .B(B[30]), .\Opção (\Opção ), .Vem1(\célula_ula_4_vai1 ),
    .Resultado(\célula_ula_32_resultado [30]));
  \Célula_ULA  \célula_ula_3  (
    .Vai1(\célula_ula_3_vai1 ), .A(A[28]), .B(B[28]), .\Opção (\Opção ), .Vem1(\célula_ula_5_vai1 ),
    .Resultado(\célula_ula_32_resultado [28]));
  \Célula_ULA  \célula_ula_4  (
    .Vai1(\célula_ula_4_vai1 ), .A(A[29]), .B(B[29]), .\Opção (\Opção ), .Vem1(\célula_ula_3_vai1 ),
    .Resultado(\célula_ula_32_resultado [29]));
  \Célula_ULA  \célula_ula_5  (
    .Vai1(\célula_ula_5_vai1 ), .A(A[27]), .B(B[27]), .\Opção (\Opção ), .Vem1(\célula_ula_6_vai1 ),
    .Resultado(\célula_ula_32_resultado [27]));
  \Célula_ULA  \célula_ula_6  (
    .Vai1(\célula_ula_6_vai1 ), .A(A[26]), .B(B[26]), .\Opção (\Opção ), .Vem1(\célula_ula_7_vai1 ),
    .Resultado(\célula_ula_32_resultado [26]));
  \Célula_ULA  \célula_ula_7  (
    .Vai1(\célula_ula_7_vai1 ), .A(A[25]), .B(B[25]), .\Opção (\Opção ), .Vem1(\célula_ula_8_vai1 ),
    .Resultado(\célula_ula_32_resultado [25]));
  \Célula_ULA  \célula_ula_8  (
    .Vai1(\célula_ula_8_vai1 ), .A(A[24]), .B(B[24]), .\Opção (\Opção ), .Vem1(\célula_ula_9_vai1 ),
    .Resultado(\célula_ula_32_resultado [24]));
  \Célula_ULA  \célula_ula_9  (
    .Vai1(\célula_ula_9_vai1 ), .A(A[23]), .B(B[23]), .\Opção (\Opção ), .Vem1(\célula_ula_10_vai1 ),
    .Resultado(\célula_ula_32_resultado [23]));
  \Célula_ULA  \célula_ula_10  (
    .Vai1(\célula_ula_10_vai1 ), .A(A[22]), .B(B[22]), .\Opção (\Opção ), .Vem1(\célula_ula_11_vai1 ),
    .Resultado(\célula_ula_32_resultado [22]));
  \Célula_ULA  \célula_ula_11  (
    .Vai1(\célula_ula_11_vai1 ), .A(A[21]), .B(B[21]), .\Opção (\Opção ), .Vem1(\célula_ula_12_vai1 ),
    .Resultado(\célula_ula_32_resultado [21]));
  \Célula_ULA  \célula_ula_12  (
    .Vai1(\célula_ula_12_vai1 ), .A(A[20]), .B(B[20]), .\Opção (\Opção ), .Vem1(\célula_ula_13_vai1 ),
    .Resultado(\célula_ula_32_resultado [20]));
  \Célula_ULA  \célula_ula_13  (
    .Vai1(\célula_ula_13_vai1 ), .A(A[19]), .B(B[19]), .\Opção (\Opção ), .Vem1(\célula_ula_14_vai1 ),
    .Resultado(\célula_ula_32_resultado [19]));
  \Célula_ULA  \célula_ula_14  (
    .Vai1(\célula_ula_14_vai1 ), .A(A[18]), .B(B[18]), .\Opção (\Opção ), .Vem1(\célula_ula_15_vai1 ),
    .Resultado(\célula_ula_32_resultado [18]));
  \Célula_ULA  \célula_ula_15  (
    .Vai1(\célula_ula_15_vai1 ), .A(A[17]), .B(B[17]), .\Opção (\Opção ), .Vem1(\célula_ula_16_vai1 ),
    .Resultado(\célula_ula_32_resultado [17]));
  \Célula_ULA  \célula_ula_16  (
    .Vai1(\célula_ula_16_vai1 ), .A(A[16]), .B(B[16]), .\Opção (\Opção ), .Vem1(\célula_ula_17_vai1 ),
    .Resultado(\célula_ula_32_resultado [16]));
  \Célula_ULA  \célula_ula_17  (
    .Vai1(\célula_ula_17_vai1 ), .A(A[15]), .B(B[15]), .\Opção (\Opção ), .Vem1(\célula_ula_18_vai1 ),
    .Resultado(\célula_ula_32_resultado [15]));
  \Célula_ULA  \célula_ula_18  (
    .Vai1(\célula_ula_18_vai1 ), .A(A[14]), .B(B[14]), .\Opção (\Opção ), .Vem1(\célula_ula_20_vai1 ),
    .Resultado(\célula_ula_32_resultado [14]));
  \Célula_ULA  \célula_ula_19  (
    .Vai1(\célula_ula_19_vai1 ), .A(A[12]), .B(B[12]), .\Opção (\Opção ), .Vem1(\célula_ula_21_vai1 ),
    .Resultado(\célula_ula_32_resultado [12]));
  \Célula_ULA  \célula_ula_20  (
    .Vai1(\célula_ula_20_vai1 ), .A(A[13]), .B(B[13]), .\Opção (\Opção ), .Vem1(\célula_ula_19_vai1 ),
    .Resultado(\célula_ula_32_resultado [13]));
  \Célula_ULA  \célula_ula_21  (
    .Vai1(\célula_ula_21_vai1 ), .A(A[11]), .B(B[11]), .\Opção (\Opção ), .Vem1(\célula_ula_22_vai1 ),
    .Resultado(\célula_ula_32_resultado [11]));
  \Célula_ULA  \célula_ula_22  (
    .Vai1(\célula_ula_22_vai1 ), .A(A[10]), .B(B[10]), .\Opção (\Opção ), .Vem1(\célula_ula_23_vai1 ),
    .Resultado(\célula_ula_32_resultado [10]));
  \Célula_ULA  \célula_ula_23  (
    .Vai1(\célula_ula_23_vai1 ), .A(A[9]), .B(B[9]), .\Opção (\Opção ), .Vem1(\célula_ula_24_vai1 ),
    .Resultado(\célula_ula_32_resultado [9]));
  \Célula_ULA  \célula_ula_24  (
    .Vai1(\célula_ula_24_vai1 ), .A(A[8]), .B(B[8]), .\Opção (\Opção ), .Vem1(\célula_ula_25_vai1 ),
    .Resultado(\célula_ula_32_resultado [8]));
  \Célula_ULA  \célula_ula_25  (
    .Vai1(\célula_ula_25_vai1 ), .A(A[7]), .B(B[7]), .\Opção (\Opção ), .Vem1(\célula_ula_26_vai1 ),
    .Resultado(\célula_ula_32_resultado [7]));
  \Célula_ULA  \célula_ula_26  (
    .Vai1(\célula_ula_26_vai1 ), .A(A[6]), .B(B[6]), .\Opção (\Opção ), .Vem1(\célula_ula_27_vai1 ),
    .Resultado(\célula_ula_32_resultado [6]));
  \Célula_ULA  \célula_ula_27  (
    .Vai1(\célula_ula_27_vai1 ), .A(A[5]), .B(B[5]), .\Opção (\Opção ), .Vem1(\célula_ula_28_vai1 ),
    .Resultado(\célula_ula_32_resultado [5]));
  \Célula_ULA  \célula_ula_28  (
    .Vai1(\célula_ula_28_vai1 ), .A(A[4]), .B(B[4]), .\Opção (\Opção ), .Vem1(\célula_ula_29_vai1 ),
    .Resultado(\célula_ula_32_resultado [4]));
  \Célula_ULA  \célula_ula_29  (
    .Vai1(\célula_ula_29_vai1 ), .A(A[3]), .B(B[3]), .\Opção (\Opção ), .Vem1(\célula_ula_30_vai1 ),
    .Resultado(\célula_ula_32_resultado [3]));
  MUX_32_bits mux_32_bits_1 (
    .in_3(detector_slt_1_out_2), .B({{31{1'b0}}, \célula_ula_32_resultado [31]}),
    .A(\célula_ula_32_resultado ), .Resultado(Resultado));
  \Detector_Subtração  \detector_subtração_1  (.Sub(\detector_subtração_1_sub ), .in_1(\Opção ));
  Detector__SLT detector_slt_1 (.in_1(\Opção ), .out_2(detector_slt_1_out_2));
  \Célula_ULA  \célula_ula_30  (
    .Vai1(\célula_ula_30_vai1 ), .A(A[2]), .B(B[2]), .\Opção (\Opção ), .Vem1(\célula_ula_31_vai1 ),
    .Resultado(\célula_ula_32_resultado [2]));
  or or_1 (or_1_out, \detector_subtração_1_sub , detector_slt_1_out_2);
  \Célula_ULA  \célula_ula_31  (
    .Vai1(\célula_ula_31_vai1 ), .A(A[1]), .B(B[1]), .\Opção (\Opção ), .Vem1(\célula_ula_32_vai1 ),
    .Resultado(\célula_ula_32_resultado [1]));
  \Célula_ULA  \célula_ula_32  (
    .Vai1(\célula_ula_32_vai1 ), .A(A[0]), .B(B[0]), .\Opção (\Opção ), .Vem1(Mux_s),
    .Resultado(\célula_ula_32_resultado [0]));
  Multiplexador_2x1 Mux (.A(1'b0), .B(1'b1), .Sel(or_1_out), .S(Mux_s));
endmodule

module OverFlowInt (
  input  in_1,
  input  in_2,
  input  in_3,
  output out_4
);

  wire xnor_1_out, xor_1_out;

  and and_1 (out_4, xnor_1_out, xor_1_out);
  xnor xnor_1 (xnor_1_out, in_1, in_2);
  xor xor_1 (xor_1_out, in_3, in_2);
endmodule

module Detector__SLT (
  input  [4:0] in_1,
  output out_2
);

  and and_1 (out_2, ~in_1[0], in_1[1], in_1[2], ~in_1[3], ~in_1[4]);  // AND_Gate
endmodule

module Maior__menor__igual (
  input  A,
  input  B,
  output IGUAL,
  output MAIOR,
  output MENOR
);

  xnor xnor_1 (IGUAL, A, B);
  and and_1 (MAIOR, A, ~B);  // AND_Gate
  and and_2 (MENOR, ~A, B);  // AND_Gate
endmodule

module ULA (
  input  [3:0] A,
  input  [3:0] B,
  input  [4:0] \Opção ,
  output [3:0] Resultado
);

  wire \célula_ula_2_vai1 , \célula_ula_3_vai1 , \célula_ula_4_vai1 , detector_slt_1_out_2,
       \detector_subtração_1_sub , multiplexador_2x1_1_s, mux_32_bits_1_p1, mux_32_bits_1_p2, or_1_out;
  wire [3:0] \célula_ula_4_resultado ;

  \Célula_ULA  \célula_ula_1  (
    .A(A[3]), .B(B[3]), .\Opção (\Opção ), .Vem1(\célula_ula_2_vai1 ), .Resultado(\célula_ula_4_resultado [3]));  // open: Vai1
  \Célula_ULA  \célula_ula_2  (
    .Vai1(\célula_ula_2_vai1 ), .A(A[2]), .B(B[2]), .\Opção (\Opção ), .Vem1(\célula_ula_3_vai1 ),
    .Resultado(\célula_ula_4_resultado [2]));
  \Célula_ULA  \célula_ula_3  (
    .Vai1(\célula_ula_3_vai1 ), .A(A[1]), .B(B[1]), .\Opção (\Opção ), .Vem1(\célula_ula_4_vai1 ),
    .Resultado(\célula_ula_4_resultado [1]));
  \Célula_ULA  \célula_ula_4  (
    .Vai1(\célula_ula_4_vai1 ), .A(A[0]), .B(B[0]), .\Opção (\Opção ), .Vem1(multiplexador_2x1_1_s),
    .Resultado(\célula_ula_4_resultado [0]));
  Multiplexador_2x1 multiplexador_2x1_1 (.A(1'b0), .B(1'b1), .Sel(or_1_out), .S(multiplexador_2x1_1_s));
  // MUX_32_bits mux_32_bits_1: pin names not known; wires that end beside it: mux_32_bits_1_p1, mux_32_bits_1_p2, Resultado
  \Detector_Subtração  \detector_subtração_1  (.Sub(\detector_subtração_1_sub ), .in_1(\Opção ));
  Detector__SLT detector_slt_1 (.in_1(\Opção ), .out_2(detector_slt_1_out_2));
  or or_1 (or_1_out, \detector_subtração_1_sub , detector_slt_1_out_2);
endmodule

module MUX_32_bits (
  input  [31:0] B,
  input  [31:0] A,
  input  in_3,
  output [31:0] Resultado
);

  Multiplexador_2x1 multiplexador_2x1_1 (.A(A[0]), .B(B[0]), .Sel(in_3), .S(Resultado[0]));
  Multiplexador_2x1 multiplexador_2x1_2 (.A(A[1]), .B(B[1]), .Sel(in_3), .S(Resultado[1]));
  Multiplexador_2x1 multiplexador_2x1_3 (.A(A[2]), .B(B[2]), .Sel(in_3), .S(Resultado[2]));
  Multiplexador_2x1 multiplexador_2x1_4 (.A(A[3]), .B(B[3]), .Sel(in_3), .S(Resultado[3]));
  Multiplexador_2x1 multiplexador_2x1_5 (.A(A[4]), .B(B[4]), .Sel(in_3), .S(Resultado[4]));
  Multiplexador_2x1 multiplexador_2x1_6 (.A(A[5]), .B(B[5]), .Sel(in_3), .S(Resultado[5]));
  Multiplexador_2x1 multiplexador_2x1_7 (.A(A[6]), .B(B[6]), .Sel(in_3), .S(Resultado[6]));
  Multiplexador_2x1 multiplexador_2x1_8 (.A(A[7]), .B(B[7]), .Sel(in_3), .S(Resultado[7]));
  Multiplexador_2x1 multiplexador_2x1_9 (.A(A[8]), .B(B[8]), .Sel(in_3), .S(Resultado[8]));
  Multiplexador_2x1 multiplexador_2x1_10 (.A(A[9]), .B(B[9]), .Sel(in_3), .S(Resultado[9]));
  Multiplexador_2x1 multiplexador_2x1_11 (.A(A[10]), .B(B[10]), .Sel(in_3), .S(Resultado[10]));
  Multiplexador_2x1 multiplexador_2x1_12 (.A(A[11]), .B(B[11]), .Sel(in_3), .S(Resultado[11]));
  Multiplexador_2x1 multiplexador_2x1_13 (.A(A[12]), .B(B[12]), .Sel(in_3), .S(Resultado[12]));
  Multiplexador_2x1 multiplexador_2x1_14 (.A(A[13]), .B(B[13]), .Sel(in_3), .S(Resultado[13]));
  Multiplexador_2x1 multiplexador_2x1_15 (.A(A[14]), .B(B[14]), .Sel(in_3), .S(Resultado[14]));
  Multiplexador_2x1 multiplexador_2x1_16 (.A(A[15]), .B(B[15]), .Sel(in_3), .S(Resultado[15]));
  Multiplexador_2x1 multiplexador_2x1_17 (.A(A[16]), .B(B[16]), .Sel(in_3), .S(Resultado[16]));
  Multiplexador_2x1 multiplexador_2x1_18 (.A(A[17]), .B(B[17]), .Sel(in_3), .S(Resultado[17]));
  Multiplexador_2x1 multiplexador_2x1_19 (.A(A[18]), .B(B[18]), .Sel(in_3), .S(Resultado[18]));
  Multiplexador_2x1 multiplexador_2x1_20 (.A(A[19]), .B(B[19]), .Sel(in_3), .S(Resultado[19]));
  Multiplexador_2x1 multiplexador_2x1_21 (.A(A[20]), .B(B[20]), .Sel(in_3), .S(Resultado[20]));
  Multiplexador_2x1 multiplexador_2x1_22 (.A(A[21]), .B(B[21]), .Sel(in_3), .S(Resultado[21]));
  Multiplexador_2x1 multiplexador_2x1_23 (.A(A[22]), .B(B[22]), .Sel(in_3), .S(Resultado[22]));
  Multiplexador_2x1 multiplexador_2x1_24 (.A(A[23]), .B(B[23]), .Sel(in_3), .S(Resultado[23]));
  Multiplexador_2x1 multiplexador_2x1_25 (.A(A[24]), .B(B[24]), .Sel(in_3), .S(Resultado[24]));
  Multiplexador_2x1 multiplexador_2x1_26 (.A(A[25]), .B(B[25]), .Sel(in_3), .S(Resultado[25]));
  Multiplexador_2x1 multiplexador_2x1_27 (.A(A[26]), .B(B[26]), .Sel(in_3), .S(Resultado[26]));
  Multiplexador_2x1 multiplexador_2x1_28 (.A(A[27]), .B(B[27]), .Sel(in_3), .S(Resultado[27]));
  Multiplexador_2x1 multiplexador_2x1_29 (.A(A[28]), .B(B[28]), .Sel(in_3), .S(Resultado[28]));
  Multiplexador_2x1 multiplexador_2x1_30 (.A(A[29]), .B(B[29]), .Sel(in_3), .S(Resultado[29]));
  Multiplexador_2x1 multiplexador_2x1_31 (.A(A[30]), .B(B[30]), .Sel(in_3), .S(Resultado[30]));
  Multiplexador_2x1 multiplexador_2x1_32 (.A(A[31]), .B(B[31]), .Sel(in_3), .S(Resultado[31]));
endmodule

module FlipFlop_D (
  input  D,
  input  CLK,
  input  Limpar,
  output Q,
  output Q1
);

  wire and_1_out, and_2_out, nand_1_out, nand_2_out, nand_3_out, not_1_out;

  not not_1 (not_1_out, D);
  and and_1 (and_1_out, D, CLK);
  nand nand_1 (nand_1_out, CLK, not_1_out);
  nand nand_2 (nand_2_out, CLK, not_1_out);
  nand nand_3 (nand_3_out, nand_1_out, Limpar);
  and and_2 (and_2_out, nand_2_out, nand_3_out);
  nand nand_4 (Q, ~and_1_out, Q1);  // NAND_Gate
  nand nand_5 (Q1, Q, and_2_out);
endmodule

module Registrador_32_bits (
  input  [31:0] Entrada,
  input  CLK,
  input  Limpar,
  output [31:0] \Saída 
);

  wire flipflop_d_4_q1;

  FlipFlop_D flipflop_d_1 (.D(Entrada[31]), .CLK(CLK), .Limpar(Limpar), .Q(\Saída [31]));  // open: Q1
  FlipFlop_D flipflop_d_2 (.D(Entrada[30]), .CLK(CLK), .Limpar(Limpar), .Q(\Saída [30]));  // open: Q1
  FlipFlop_D flipflop_d_3 (.D(Entrada[29]), .CLK(CLK), .Limpar(Limpar), .Q(\Saída [29]));  // open: Q1
  FlipFlop_D flipflop_d_4 (.D(Entrada[28]), .CLK(CLK), .Limpar(Limpar), .Q(\Saída [28]), .Q1(flipflop_d_4_q1));
  FlipFlop_D flipflop_d_5 (.D(Entrada[27]), .CLK(CLK), .Limpar(Limpar), .Q(\Saída [27]));  // open: Q1
  FlipFlop_D flipflop_d_6 (.D(Entrada[25]), .CLK(CLK), .Limpar(Limpar), .Q(\Saída [25]));  // open: Q1
  FlipFlop_D flipflop_d_7 (.D(Entrada[26]), .CLK(CLK), .Limpar(Limpar), .Q(\Saída [26]));  // open: Q1
  FlipFlop_D flipflop_d_8 (.D(Entrada[24]), .CLK(CLK), .Limpar(Limpar), .Q(\Saída [24]));  // open: Q1
  FlipFlop_D flipflop_d_9 (.D(Entrada[23]), .CLK(CLK), .Limpar(Limpar), .Q(\Saída [23]));  // open: Q1
  FlipFlop_D flipflop_d_10 (.D(Entrada[22]), .CLK(CLK), .Limpar(Limpar), .Q(\Saída [22]));  // open: Q1
  FlipFlop_D flipflop_d_11 (.D(Entrada[21]), .CLK(CLK), .Limpar(Limpar), .Q(\Saída [21]));  // open: Q1
  FlipFlop_D flipflop_d_12 (.D(Entrada[20]), .CLK(CLK), .Limpar(Limpar), .Q(\Saída [20]));  // open: Q1
  FlipFlop_D flipflop_d_13 (.D(Entrada[19]), .CLK(CLK), .Limpar(Limpar), .Q(\Saída [19]));  // open: Q1
  FlipFlop_D flipflop_d_14 (.D(Entrada[18]), .CLK(CLK), .Limpar(Limpar), .Q(\Saída [18]));  // open: Q1
  FlipFlop_D flipflop_d_15 (.D(Entrada[17]), .CLK(CLK), .Limpar(Limpar), .Q(\Saída [17]));  // open: Q1
  FlipFlop_D flipflop_d_16 (.D(Entrada[16]), .CLK(CLK), .Limpar(Limpar), .Q(\Saída [16]));  // open: Q1
  FlipFlop_D flipflop_d_17 (.D(Entrada[15]), .CLK(CLK), .Limpar(Limpar), .Q(\Saída [15]));  // open: Q1
  FlipFlop_D flipflop_d_18 (.D(Entrada[14]), .CLK(CLK), .Limpar(Limpar), .Q(\Saída [14]));  // open: Q1
  FlipFlop_D flipflop_d_19 (.D(Entrada[13]), .CLK(CLK), .Limpar(Limpar), .Q(\Saída [13]));  // open: Q1
  FlipFlop_D flipflop_d_20 (.D(Entrada[12]), .CLK(CLK), .Limpar(Limpar), .Q(\Saída [12]));  // open: Q1
  FlipFlop_D flipflop_d_21 (.D(Entrada[11]), .CLK(CLK), .Limpar(Limpar), .Q(\Saída [11]));  // open: Q1
  FlipFlop_D flipflop_d_22 (.D(Entrada[10]), .CLK(CLK), .Limpar(Limpar), .Q(\Saída [10]));  // open: Q1
  FlipFlop_D flipflop_d_23 (.D(Entrada[9]), .CLK(CLK), .Limpar(Limpar), .Q(\Saída [9]));  // open: Q1
  FlipFlop_D flipflop_d_24 (.D(Entrada[8]), .CLK(CLK), .Limpar(Limpar), .Q(\Saída [8]));  // open: Q1
  FlipFlop_D flipflop_d_25 (.D(Entrada[7]), .CLK(CLK), .Limpar(Limpar), .Q(\Saída [7]));  // open: Q1
  FlipFlop_D flipflop_d_26 (.D(Entrada[6]), .CLK(CLK), .Limpar(Limpar), .Q(\Saída [6]));  // open: Q1
  FlipFlop_D flipflop_d_27 (.D(Entrada[5]), .CLK(CLK), .Limpar(Limpar), .Q(\Saída [5]));  // open: Q1
  FlipFlop_D flipflop_d_28 (.D(Entrada[4]), .CLK(CLK), .Limpar(Limpar), .Q(\Saída [4]));  // open: Q1
  FlipFlop_D flipflop_d_29 (.D(Entrada[3]), .CLK(CLK), .Limpar(Limpar), .Q(\Saída [3]));  // open: Q1
  FlipFlop_D flipflop_d_30 (.D(Entrada[2]), .CLK(CLK), .Limpar(Limpar), .Q(\Saída [2]));  // open: Q1
  FlipFlop_D flipflop_d_31 (.D(Entrada[1]), .CLK(CLK), .Limpar(Limpar), .Q(\Saída [1]));  // open: Q1
  FlipFlop_D flipflop_d_32 (.D(Entrada[0]), .CLK(CLK), .Limpar(Limpar), .Q(\Saída [0]));  // open: Q1
endmodule

module Banco_Registrador_32_bits (
  input  [4:0] Registro2,
  input  LImpar,
  input  Salvar,
  input  [4:0] Destino,
  input  [4:0] Registro1,
  input  [31:0] Entrada,
  output [31:0] \Saída1 ,
  output [31:0] \Saída2 
);

  wire demultiplexer_1_out0, demultiplexer_1_out1, demultiplexer_1_out2, demultiplexer_1_out3,
       demultiplexer_1_out4, demultiplexer_1_out5, demultiplexer_1_out6, demultiplexer_1_out7,
       demultiplexer_1_out8, demultiplexer_1_out9, demultiplexer_1_out10, demultiplexer_1_out11,
       demultiplexer_1_out12, demultiplexer_1_out13, demultiplexer_1_out14, demultiplexer_1_out15,
       demultiplexer_1_out16, demultiplexer_1_out17, demultiplexer_1_out18, demultiplexer_1_out19,
       demultiplexer_1_out20, demultiplexer_1_out21, demultiplexer_1_out22, demultiplexer_1_out23,
       demultiplexer_1_out24, demultiplexer_1_out25, demultiplexer_1_out26, demultiplexer_1_out27,
       demultiplexer_1_out28, demultiplexer_1_out29, demultiplexer_1_out30, demultiplexer_1_out31;
  wire [31:0] \registrador_32_bits_1_saída , \registrador_32_bits_2_saída , \registrador_32_bits_3_saída ,
       \registrador_32_bits_4_saída , \registrador_32_bits_5_saída , \registrador_32_bits_6_saída ,
       \registrador_32_bits_7_saída , \registrador_32_bits_8_saída , \registrador_32_bits_9_saída ,
       \registrador_32_bits_10_saída , \registrador_32_bits_11_saída , \registrador_32_bits_12_saída ,
       \registrador_32_bits_13_saída , \registrador_32_bits_14_saída , \registrador_32_bits_15_saída ,
       \registrador_32_bits_16_saída , \registrador_32_bits_17_saída , \registrador_32_bits_18_saída ,
       \registrador_32_bits_19_saída , \registrador_32_bits_20_saída , \registrador_32_bits_21_saída ,
       \registrador_32_bits_22_saída , \registrador_32_bits_23_saída , \registrador_32_bits_24_saída ,
       \registrador_32_bits_25_saída , \registrador_32_bits_26_saída , \registrador_32_bits_27_saída ,
       \registrador_32_bits_28_saída , \registrador_32_bits_29_saída , \registrador_32_bits_30_saída ,
       \registrador_32_bits_31_saída , \registrador_32_bits_32_saída ;

  Demultiplexer #(.select(5), .enable("false")) demultiplexer_1 (
    .out0(demultiplexer_1_out0), .out1(demultiplexer_1_out1), .out2(demultiplexer_1_out2),
    .out3(demultiplexer_1_out3), .out4(demultiplexer_1_out4), .out5(demultiplexer_1_out5),
    .out6(demultiplexer_1_out6), .out7(demultiplexer_1_out7), .out8(demultiplexer_1_out8),
    .out9(demultiplexer_1_out9), .out10(demultiplexer_1_out10), .out11(demultiplexer_1_out11),
    .out12(demultiplexer_1_out12), .out13(demultiplexer_1_out13), .out14(demultiplexer_1_out14),
    .out15(demultiplexer_1_out15), .out16(demultiplexer_1_out16), .out17(demultiplexer_1_out17),
    .out18(demultiplexer_1_out18), .out19(demultiplexer_1_out19), .out20(demultiplexer_1_out20),
    .out21(demultiplexer_1_out21), .out22(demultiplexer_1_out22), .out23(demultiplexer_1_out23),
    .out24(demultiplexer_1_out24), .out25(demultiplexer_1_out25), .out26(demultiplexer_1_out26),
    .out27(demultiplexer_1_out27), .out28(demultiplexer_1_out28), .out29(demultiplexer_1_out29),
    .out30(demultiplexer_1_out30), .out31(demultiplexer_1_out31), .in(Salvar), .sel(Destino));
  Registrador_32_bits registrador_32_bits_1 (
    .Entrada(Entrada), .CLK(demultiplexer_1_out0), .Limpar(LImpar), .\Saída (\registrador_32_bits_1_saída ));
  Registrador_32_bits registrador_32_bits_2 (
    .Entrada(Entrada), .CLK(demultiplexer_1_out1), .Limpar(LImpar), .\Saída (\registrador_32_bits_2_saída ));
  Registrador_32_bits registrador_32_bits_3 (
    .Entrada(Entrada), .CLK(demultiplexer_1_out2), .Limpar(LImpar), .\Saída (\registrador_32_bits_3_saída ));
  Registrador_32_bits registrador_32_bits_4 (
    .Entrada(Entrada), .CLK(demultiplexer_1_out3), .Limpar(LImpar), .\Saída (\registrador_32_bits_4_saída ));
  Registrador_32_bits registrador_32_bits_5 (
    .Entrada(Entrada), .CLK(demultiplexer_1_out4), .Limpar(LImpar), .\Saída (\registrador_32_bits_5_saída ));
  Registrador_32_bits registrador_32_bits_6 (
    .Entrada(Entrada), .CLK(demultiplexer_1_out5), .Limpar(LImpar), .\Saída (\registrador_32_bits_6_saída ));
  Registrador_32_bits registrador_32_bits_7 (
    .Entrada(Entrada), .CLK(demultiplexer_1_out6), .Limpar(LImpar), .\Saída (\registrador_32_bits_7_saída ));
  Registrador_32_bits registrador_32_bits_8 (
    .Entrada(Entrada), .CLK(demultiplexer_1_out7), .Limpar(LImpar), .\Saída (\registrador_32_bits_8_saída ));
  Registrador_32_bits registrador_32_bits_9 (
    .Entrada(Entrada), .CLK(demultiplexer_1_out8), .Limpar(LImpar), .\Saída (\registrador_32_bits_9_saída ));
  Registrador_32_bits registrador_32_bits_10 (
    .Entrada(Entrada), .CLK(demultiplexer_1_out9), .Limpar(LImpar), .\Saída (\registrador_32_bits_10_saída ));
  Registrador_32_bits registrador_32_bits_11 (
    .Entrada(Entrada), .CLK(demultiplexer_1_out10), .Limpar(LImpar), .\Saída (\registrador_32_bits_11_saída ));
  Registrador_32_bits registrador_32_bits_12 (
    .Entrada(Entrada), .CLK(demultiplexer_1_out11), .Limpar(LImpar), .\Saída (\registrador_32_bits_12_saída ));
  Registrador_32_bits registrador_32_bits_13 (
    .Entrada(Entrada), .CLK(demultiplexer_1_out12), .Limpar(LImpar), .\Saída (\registrador_32_bits_13_saída ));
  Registrador_32_bits registrador_32_bits_14 (
    .Entrada(Entrada), .CLK(demultiplexer_1_out13), .Limpar(LImpar), .\Saída (\registrador_32_bits_14_saída ));
  Registrador_32_bits registrador_32_bits_15 (
    .Entrada(Entrada), .CLK(demultiplexer_1_out14), .Limpar(LImpar), .\Saída (\registrador_32_bits_15_saída ));
  Registrador_32_bits registrador_32_bits_16 (
    .Entrada(Entrada), .CLK(demultiplexer_1_out15), .Limpar(LImpar), .\Saída (\registrador_32_bits_16_saída ));
  Registrador_32_bits registrador_32_bits_17 (
    .Entrada(Entrada), .CLK(demultiplexer_1_out16), .Limpar(LImpar), .\Saída (\registrador_32_bits_17_saída ));
  Registrador_32_bits registrador_32_bits_18 (
    .Entrada(Entrada), .CLK(demultiplexer_1_out17), .Limpar(LImpar), .\Saída (\registrador_32_bits_18_saída ));
  Registrador_32_bits registrador_32_bits_19 (
    .Entrada(Entrada), .CLK(demultiplexer_1_out18), .Limpar(LImpar), .\Saída (\registrador_32_bits_19_saída ));
  Registrador_32_bits registrador_32_bits_20 (
    .Entrada(Entrada), .CLK(demultiplexer_1_out19), .Limpar(LImpar), .\Saída (\registrador_32_bits_20_saída ));
  Registrador_32_bits registrador_32_bits_21 (
    .Entrada(Entrada), .CLK(demultiplexer_1_out20), .Limpar(LImpar), .\Saída (\registrador_32_bits_21_saída ));
  Registrador_32_bits registrador_32_bits_22 (
    .Entrada(Entrada), .CLK(demultiplexer_1_out21), .Limpar(LImpar), .\Saída (\registrador_32_bits_22_saída ));
  Registrador_32_bits registrador_32_bits_23 (
    .Entrada(Entrada), .CLK(demultiplexer_1_out22), .Limpar(LImpar), .\Saída (\registrador_32_bits_23_saída ));
  Registrador_32_bits registrador_32_bits_24 (
    .Entrada(Entrada), .CLK(demultiplexer_1_out23), .Limpar(LImpar), .\Saída (\registrador_32_bits_24_saída ));
  Registrador_32_bits registrador_32_bits_25 (
    .Entrada(Entrada), .CLK(demultiplexer_1_out24), .Limpar(LImpar), .\Saída (\registrador_32_bits_25_saída ));
  Registrador_32_bits registrador_32_bits_26 (
    .Entrada(Entrada), .CLK(demultiplexer_1_out25), .Limpar(LImpar), .\Saída (\registrador_32_bits_26_saída ));
  Registrador_32_bits registrador_32_bits_27 (
    .Entrada(Entrada), .CLK(demultiplexer_1_out26), .Limpar(LImpar), .\Saída (\registrador_32_bits_27_saída ));
  Registrador_32_bits registrador_32_bits_28 (
    .Entrada(Entrada), .CLK(demultiplexer_1_out27), .Limpar(LImpar), .\Saída (\registrador_32_bits_28_saída ));
  Registrador_32_bits registrador_32_bits_29 (
    .Entrada(Entrada), .CLK(demultiplexer_1_out28), .Limpar(LImpar), .\Saída (\registrador_32_bits_29_saída ));
  Registrador_32_bits registrador_32_bits_30 (
    .Entrada(Entrada), .CLK(demultiplexer_1_out29), .Limpar(LImpar), .\Saída (\registrador_32_bits_30_saída ));
  Registrador_32_bits registrador_32_bits_31 (
    .Entrada(Entrada), .CLK(demultiplexer_1_out30), .Limpar(LImpar), .\Saída (\registrador_32_bits_31_saída ));
  Registrador_32_bits registrador_32_bits_32 (
    .Entrada(Entrada), .CLK(demultiplexer_1_out31), .Limpar(LImpar), .\Saída (\registrador_32_bits_32_saída ));
  Multiplexer #(.select(5), .width(32), .enable("false")) multiplexer_1 (
    .in0(\registrador_32_bits_1_saída ), .in1(\registrador_32_bits_2_saída ),
    .in2(\registrador_32_bits_3_saída ), .in3(\registrador_32_bits_4_saída ),
    .in4(\registrador_32_bits_5_saída ), .in5(\registrador_32_bits_6_saída ),
    .in6(\registrador_32_bits_7_saída ), .in7(\registrador_32_bits_8_saída ),
    .in8(\registrador_32_bits_9_saída ), .in9(\registrador_32_bits_10_saída ),
    .in10(\registrador_32_bits_11_saída ), .in11(\registrador_32_bits_12_saída ),
    .in12(\registrador_32_bits_13_saída ), .in13(\registrador_32_bits_14_saída ),
    .in14(\registrador_32_bits_15_saída ), .in15(\registrador_32_bits_16_saída ),
    .in16(\registrador_32_bits_17_saída ), .in17(\registrador_32_bits_18_saída ),
    .in18(\registrador_32_bits_19_saída ), .in19(\registrador_32_bits_20_saída ),
    .in20(\registrador_32_bits_21_saída ), .in21(\registrador_32_bits_22_saída ),
    .in22(\registrador_32_bits_23_saída ), .in23(\registrador_32_bits_24_saída ),
    .in24(\registrador_32_bits_25_saída ), .in25(\registrador_32_bits_26_saída ),
    .in26(\registrador_32_bits_27_saída ), .in27(\registrador_32_bits_28_saída ),
    .in28(\registrador_32_bits_29_saída ), .in29(\registrador_32_bits_30_saída ),
    .in30(\registrador_32_bits_31_saída ), .in31(\registrador_32_bits_32_saída ), .out(\Saída1 ),
    .sel(Registro2));
  Multiplexer #(.select(5), .width(32), .enable("false")) multiplexer_2 (
    .in0(\registrador_32_bits_1_saída ), .in1(\registrador_32_bits_2_saída ),
    .in2(\registrador_32_bits_3_saída ), .in3(\registrador_32_bits_4_saída ),
    .in4(\registrador_32_bits_5_saída ), .in5(\registrador_32_bits_6_saída ),
    .in6(\registrador_32_bits_7_saída ), .in7(\registrador_32_bits_8_saída ),
    .in8(\registrador_32_bits_9_saída ), .in9(\registrador_32_bits_10_saída ),
    .in10(\registrador_32_bits_11_saída ), .in11(\registrador_32_bits_12_saída ),
    .in12(\registrador_32_bits_13_saída ), .in13(\registrador_32_bits_14_saída ),
    .in14(\registrador_32_bits_15_saída ), .in15(\registrador_32_bits_16_saída ),
    .in16(\registrador_32_bits_17_saída ), .in17(\registrador_32_bits_18_saída ),
    .in18(\registrador_32_bits_19_saída ), .in19(\registrador_32_bits_20_saída ),
    .in20(\registrador_32_bits_21_saída ), .in21(\registrador_32_bits_22_saída ),
    .in22(\registrador_32_bits_23_saída ), .in23(\registrador_32_bits_24_saída ),
    .in24(\registrador_32_bits_25_saída ), .in25(\registrador_32_bits_26_saída ),
    .in26(\registrador_32_bits_27_saída ), .in27(\registrador_32_bits_28_saída ),
    .in28(\registrador_32_bits_29_saída ), .in29(\registrador_32_bits_30_saída ),
    .in30(\registrador_32_bits_31_saída ), .in31(\registrador_32_bits_32_saída ), .out(\Saída2 ),
    .sel(Registro1));
endmodule

module Registrador_32_bits_2 (
  input  [31:0] DataIn,
  input  CLK,
  input  Clear,
  output [31:0] DataOut
);

  D_Flip_Flop d_ff_1 (.clk(CLK), .D(DataIn[31]), .Q(DataOut[31]), .reset(Clear));  // open: Qn, preset, en
  D_Flip_Flop d_ff_2 (.clk(CLK), .D(DataIn[30]), .Q(DataOut[30]), .reset(Clear));  // open: Qn, preset, en
  D_Flip_Flop d_ff_3 (.clk(CLK), .D(DataIn[29]), .Q(DataOut[29]), .reset(Clear));  // open: Qn, preset, en
  D_Flip_Flop d_ff_4 (.clk(CLK), .D(DataIn[28]), .Q(DataOut[28]), .reset(Clear));  // open: Qn, preset, en
  D_Flip_Flop d_ff_5 (.clk(CLK), .D(DataIn[27]), .Q(DataOut[27]), .reset(Clear));  // open: Qn, preset, en
  D_Flip_Flop d_ff_6 (.clk(CLK), .D(DataIn[25]), .Q(DataOut[25]), .reset(Clear));  // open: Qn, preset, en
  D_Flip_Flop d_ff_7 (.clk(CLK), .D(DataIn[26]), .Q(DataOut[26]), .reset(Clear));  // open: Qn, preset, en
  D_Flip_Flop d_ff_8 (.clk(CLK), .D(DataIn[24]), .Q(DataOut[24]), .reset(Clear));  // open: Qn, preset, en
  D_Flip_Flop d_ff_9 (.clk(CLK), .D(DataIn[23]), .Q(DataOut[23]), .reset(Clear));  // open: Qn, preset, en
  D_Flip_Flop d_ff_10 (.clk(CLK), .D(DataIn[22]), .Q(DataOut[22]), .reset(Clear));  // open: Qn, preset, en
  D_Flip_Flop d_ff_11 (.clk(CLK), .D(DataIn[21]), .Q(DataOut[21]), .reset(Clear));  // open: Qn, preset, en
  D_Flip_Flop d_ff_12 (.clk(CLK), .D(DataIn[20]), .Q(DataOut[20]), .reset(Clear));  // open: Qn, preset, en
  D_Flip_Flop d_ff_13 (.clk(CLK), .D(DataIn[19]), .Q(DataOut[19]), .reset(Clear));  // open: Qn, preset, en
  D_Flip_Flop d_ff_14 (.clk(CLK), .D(DataIn[17]), .Q(DataOut[17]), .reset(Clear));  // open: Qn, preset, en
  D_Flip_Flop d_ff_15 (.clk(CLK), .D(DataIn[18]), .Q(DataOut[18]), .reset(Clear));  // open: Qn, preset, en
  D_Flip_Flop d_ff_16 (.clk(CLK), .D(DataIn[16]), .Q(DataOut[16]), .reset(Clear));  // open: Qn, preset, en
  D_Flip_Flop d_ff_17 (.clk(CLK), .D(DataIn[15]), .Q(DataOut[15]));  // open: Qn, preset, en, reset
  D_Flip_Flop d_ff_18 (.clk(CLK), .D(DataIn[14]), .Q(DataOut[14]), .reset(Clear));  // open: Qn, preset, en
  D_Flip_Flop d_ff_19 (.clk(CLK), .D(DataIn[13]), .Q(DataOut[13]), .reset(Clear));  // open: Qn, preset, en
  D_Flip_Flop d_ff_20 (.clk(CLK), .D(DataIn[12]), .Q(DataOut[12]), .reset(Clear));  // open: Qn, preset, en
  D_Flip_Flop d_ff_21 (.clk(CLK), .D(DataIn[11]), .Q(DataOut[11]), .reset(Clear));  // open: Qn, preset, en
  D_Flip_Flop d_ff_22 (.clk(CLK), .D(DataIn[9]), .Q(DataOut[9]), .reset(Clear));  // open: Qn, preset, en
  D_Flip_Flop d_ff_23 (.clk(CLK), .D(DataIn[10]), .Q(DataOut[10]), .reset(Clear));  // open: Qn, preset, en
  D_Flip_Flop d_ff_24 (.clk(CLK), .D(DataIn[8]), .Q(DataOut[8]), .reset(Clear));  // open: Qn, preset, en
  D_Flip_Flop d_ff_25 (.clk(CLK), .D(DataIn[7]), .Q(DataOut[7]), .reset(Clear));  // open: Qn, preset, en
  D_Flip_Flop d_ff_26 (.clk(CLK), .D(DataIn[6]), .Q(DataOut[6]), .reset(Clear));  // open: Qn, preset, en
  D_Flip_Flop d_ff_27 (.clk(CLK), .D(DataIn[5]), .Q(DataOut[5]), .reset(Clear));  // open: Qn, preset, en
  D_Flip_Flop d_ff_28 (.clk(CLK), .D(DataIn[4]), .Q(DataOut[4]), .reset(Clear));  // open: Qn, preset, en
  D_Flip_Flop d_ff_29 (.clk(CLK), .D(DataIn[3]), .Q(DataOut[3]), .reset(Clear));  // open: Qn, preset, en
  D_Flip_Flop d_ff_30 (.clk(CLK), .D(DataIn[2]), .Q(DataOut[2]), .reset(Clear));  // open: Qn, preset, en
  D_Flip_Flop d_ff_31 (.clk(CLK), .D(DataIn[1]), .Q(DataOut[1]), .reset(Clear));  // open: Qn, preset, en
  D_Flip_Flop d_ff_32 (.clk(CLK), .D(DataIn[0]), .Q(DataOut[0]), .reset(Clear));  // open: Qn, preset, en
endmodule

module Banco_Registrador_32_bits_2 (
  input  [4:0] Registro2,
  input  LImpar,
  input  Salvar,
  input  [4:0] Destino,
  input  [4:0] Registro1,
  input  [31:0] Entrada,
  output [31:0] \Saída1 ,
  output [31:0] \Saída2 
);

  wire demultiplexer_1_out0, demultiplexer_1_out1, demultiplexer_1_out2, demultiplexer_1_out3,
       demultiplexer_1_out4, demultiplexer_1_out5, demultiplexer_1_out6, demultiplexer_1_out7,
       demultiplexer_1_out8, demultiplexer_1_out9, demultiplexer_1_out10, demultiplexer_1_out11,
       demultiplexer_1_out12, demultiplexer_1_out13, demultiplexer_1_out14, demultiplexer_1_out15,
       demultiplexer_1_out16, demultiplexer_1_out17, demultiplexer_1_out18, demultiplexer_1_out19,
       demultiplexer_1_out20, demultiplexer_1_out21, demultiplexer_1_out22, demultiplexer_1_out23,
       demultiplexer_1_out24, demultiplexer_1_out25, demultiplexer_1_out26, demultiplexer_1_out27,
       demultiplexer_1_out28, demultiplexer_1_out29, demultiplexer_1_out30, demultiplexer_1_out31;
  wire [31:0] registrador_32_bits_2_1_dataout, registrador_32_bits_2_2_dataout,
       registrador_32_bits_2_3_dataout, registrador_32_bits_2_4_dataout, registrador_32_bits_2_5_dataout,
       registrador_32_bits_2_6_dataout, registrador_32_bits_2_7_dataout, registrador_32_bits_2_8_dataout,
       registrador_32_bits_2_9_dataout, registrador_32_bits_2_10_dataout, registrador_32_bits_2_11_dataout,
       registrador_32_bits_2_12_dataout, registrador_32_bits_2_13_dataout, registrador_32_bits_2_14_dataout,
       registrador_32_bits_2_15_dataout, registrador_32_bits_2_16_dataout, registrador_32_bits_2_17_dataout,
       registrador_32_bits_2_18_dataout, registrador_32_bits_2_19_dataout, registrador_32_bits_2_20_dataout,
       registrador_32_bits_2_21_dataout, registrador_32_bits_2_22_dataout, registrador_32_bits_2_23_dataout,
       registrador_32_bits_2_24_dataout, registrador_32_bits_2_25_dataout, registrador_32_bits_2_26_dataout,
       registrador_32_bits_2_27_dataout, registrador_32_bits_2_28_dataout, registrador_32_bits_2_29_dataout,
       registrador_32_bits_2_30_dataout, registrador_32_bits_2_31_dataout, registrador_32_bits_2_32_dataout;

  Demultiplexer #(.select(5), .enable("false")) demultiplexer_1 (
    .out0(demultiplexer_1_out0), .out1(demultiplexer_1_out1), .out2(demultiplexer_1_out2),
    .out3(demultiplexer_1_out3), .out4(demultiplexer_1_out4), .out5(demultiplexer_1_out5),
    .out6(demultiplexer_1_out6), .out7(demultiplexer_1_out7), .out8(demultiplexer_1_out8),
    .out9(demultiplexer_1_out9), .out10(demultiplexer_1_out10), .out11(demultiplexer_1_out11),
    .out12(demultiplexer_1_out12), .out13(demultiplexer_1_out13), .out14(demultiplexer_1_out14),
    .out15(demultiplexer_1_out15), .out16(demultiplexer_1_out16), .out17(demultiplexer_1_out17),
    .out18(demultiplexer_1_out18), .out19(demultiplexer_1_out19), .out20(demultiplexer_1_out20),
    .out21(demultiplexer_1_out21), .out22(demultiplexer_1_out22), .out23(demultiplexer_1_out23),
    .out24(demultiplexer_1_out24), .out25(demultiplexer_1_out25), .out26(demultiplexer_1_out26),
    .out27(demultiplexer_1_out27), .out28(demultiplexer_1_out28), .out29(demultiplexer_1_out29),
    .out30(demultiplexer_1_out30), .out31(demultiplexer_1_out31), .in(Salvar), .sel(Destino));
  Registrador_32_bits_2 registrador_32_bits_2_1 (
    .DataIn(Entrada), .CLK(demultiplexer_1_out0), .Clear(LImpar), .DataOut(registrador_32_bits_2_1_dataout));
  Registrador_32_bits_2 registrador_32_bits_2_2 (
    .DataIn(Entrada), .CLK(demultiplexer_1_out1), .Clear(LImpar), .DataOut(registrador_32_bits_2_2_dataout));
  Registrador_32_bits_2 registrador_32_bits_2_3 (
    .DataIn(Entrada), .CLK(demultiplexer_1_out2), .Clear(LImpar), .DataOut(registrador_32_bits_2_3_dataout));
  Registrador_32_bits_2 registrador_32_bits_2_4 (
    .DataIn(Entrada), .CLK(demultiplexer_1_out3), .Clear(LImpar), .DataOut(registrador_32_bits_2_4_dataout));
  Registrador_32_bits_2 registrador_32_bits_2_5 (
    .DataIn(Entrada), .CLK(demultiplexer_1_out4), .Clear(LImpar), .DataOut(registrador_32_bits_2_5_dataout));
  Registrador_32_bits_2 registrador_32_bits_2_6 (
    .DataIn(Entrada), .CLK(demultiplexer_1_out5), .Clear(LImpar), .DataOut(registrador_32_bits_2_6_dataout));
  Registrador_32_bits_2 registrador_32_bits_2_7 (
    .DataIn(Entrada), .CLK(demultiplexer_1_out6), .Clear(LImpar), .DataOut(registrador_32_bits_2_7_dataout));
  Registrador_32_bits_2 registrador_32_bits_2_8 (
    .DataIn(Entrada), .CLK(demultiplexer_1_out7), .Clear(LImpar), .DataOut(registrador_32_bits_2_8_dataout));
  Registrador_32_bits_2 registrador_32_bits_2_9 (
    .DataIn(Entrada), .CLK(demultiplexer_1_out8), .Clear(LImpar), .DataOut(registrador_32_bits_2_9_dataout));
  Registrador_32_bits_2 registrador_32_bits_2_10 (
    .DataIn(Entrada), .CLK(demultiplexer_1_out9), .Clear(LImpar), .DataOut(registrador_32_bits_2_10_dataout));
  Registrador_32_bits_2 registrador_32_bits_2_11 (
    .DataIn(Entrada), .CLK(demultiplexer_1_out10), .Clear(LImpar), .DataOut(registrador_32_bits_2_11_dataout));
  Registrador_32_bits_2 registrador_32_bits_2_12 (
    .DataIn(Entrada), .CLK(demultiplexer_1_out11), .Clear(LImpar), .DataOut(registrador_32_bits_2_12_dataout));
  Registrador_32_bits_2 registrador_32_bits_2_13 (
    .DataIn(Entrada), .CLK(demultiplexer_1_out12), .Clear(LImpar), .DataOut(registrador_32_bits_2_13_dataout));
  Registrador_32_bits_2 registrador_32_bits_2_14 (
    .DataIn(Entrada), .CLK(demultiplexer_1_out13), .Clear(LImpar), .DataOut(registrador_32_bits_2_14_dataout));
  Registrador_32_bits_2 registrador_32_bits_2_15 (
    .DataIn(Entrada), .CLK(demultiplexer_1_out14), .Clear(LImpar), .DataOut(registrador_32_bits_2_15_dataout));
  Registrador_32_bits_2 registrador_32_bits_2_16 (
    .DataIn(Entrada), .CLK(demultiplexer_1_out15), .Clear(LImpar), .DataOut(registrador_32_bits_2_16_dataout));
  Registrador_32_bits_2 registrador_32_bits_2_17 (
    .DataIn(Entrada), .CLK(demultiplexer_1_out16), .Clear(LImpar), .DataOut(registrador_32_bits_2_17_dataout));
  Registrador_32_bits_2 registrador_32_bits_2_18 (
    .DataIn(Entrada), .CLK(demultiplexer_1_out17), .Clear(LImpar), .DataOut(registrador_32_bits_2_18_dataout));
  Registrador_32_bits_2 registrador_32_bits_2_19 (
    .DataIn(Entrada), .CLK(demultiplexer_1_out18), .Clear(LImpar), .DataOut(registrador_32_bits_2_19_dataout));
  Registrador_32_bits_2 registrador_32_bits_2_20 (
    .DataIn(Entrada), .CLK(demultiplexer_1_out19), .Clear(LImpar), .DataOut(registrador_32_bits_2_20_dataout));
  Registrador_32_bits_2 registrador_32_bits_2_21 (
    .DataIn(Entrada), .CLK(demultiplexer_1_out20), .Clear(LImpar), .DataOut(registrador_32_bits_2_21_dataout));
  Registrador_32_bits_2 registrador_32_bits_2_22 (
    .DataIn(Entrada), .CLK(demultiplexer_1_out21), .Clear(LImpar), .DataOut(registrador_32_bits_2_22_dataout));
  Registrador_32_bits_2 registrador_32_bits_2_23 (
    .DataIn(Entrada), .CLK(demultiplexer_1_out22), .Clear(LImpar), .DataOut(registrador_32_bits_2_23_dataout));
  Registrador_32_bits_2 registrador_32_bits_2_24 (
    .DataIn(Entrada), .CLK(demultiplexer_1_out23), .Clear(LImpar), .DataOut(registrador_32_bits_2_24_dataout));
  Registrador_32_bits_2 registrador_32_bits_2_25 (
    .DataIn(Entrada), .CLK(demultiplexer_1_out24), .Clear(LImpar), .DataOut(registrador_32_bits_2_25_dataout));
  Registrador_32_bits_2 registrador_32_bits_2_26 (
    .DataIn(Entrada), .CLK(demultiplexer_1_out25), .Clear(LImpar), .DataOut(registrador_32_bits_2_26_dataout));
  Registrador_32_bits_2 registrador_32_bits_2_27 (
    .DataIn(Entrada), .CLK(demultiplexer_1_out26), .Clear(LImpar), .DataOut(registrador_32_bits_2_27_dataout));
  Registrador_32_bits_2 registrador_32_bits_2_28 (
    .DataIn(Entrada), .CLK(demultiplexer_1_out27), .Clear(LImpar), .DataOut(registrador_32_bits_2_28_dataout));
  Registrador_32_bits_2 registrador_32_bits_2_29 (
    .DataIn(Entrada), .CLK(demultiplexer_1_out28), .Clear(LImpar), .DataOut(registrador_32_bits_2_29_dataout));
  Registrador_32_bits_2 registrador_32_bits_2_30 (
    .DataIn(Entrada), .CLK(demultiplexer_1_out29), .Clear(LImpar), .DataOut(registrador_32_bits_2_30_dataout));
  Registrador_32_bits_2 registrador_32_bits_2_31 (
    .DataIn(Entrada), .CLK(demultiplexer_1_out30), .Clear(LImpar), .DataOut(registrador_32_bits_2_31_dataout));
  Registrador_32_bits_2 registrador_32_bits_2_32 (
    .DataIn(Entrada), .CLK(demultiplexer_1_out31), .Clear(LImpar), .DataOut(registrador_32_bits_2_32_dataout));
  Multiplexer #(.select(5), .width(32), .enable("false")) multiplexer_1 (
    .in0(registrador_32_bits_2_1_dataout), .in1(registrador_32_bits_2_2_dataout),
    .in2(registrador_32_bits_2_3_dataout), .in3(registrador_32_bits_2_4_dataout),
    .in4(registrador_32_bits_2_5_dataout), .in5(registrador_32_bits_2_6_dataout),
    .in6(registrador_32_bits_2_7_dataout), .in7(registrador_32_bits_2_8_dataout),
    .in8(registrador_32_bits_2_9_dataout), .in9(registrador_32_bits_2_10_dataout),
    .in10(registrador_32_bits_2_11_dataout), .in11(registrador_32_bits_2_12_dataout),
    .in12(registrador_32_bits_2_13_dataout), .in13(registrador_32_bits_2_14_dataout),
    .in14(registrador_32_bits_2_15_dataout), .in15(registrador_32_bits_2_16_dataout),
    .in16(registrador_32_bits_2_17_dataout), .in17(registrador_32_bits_2_18_dataout),
    .in18(registrador_32_bits_2_19_dataout), .in19(registrador_32_bits_2_20_dataout),
    .in20(registrador_32_bits_2_21_dataout), .in21(registrador_32_bits_2_22_dataout),
    .in22(registrador_32_bits_2_23_dataout), .in23(registrador_32_bits_2_24_dataout),
    .in24(registrador_32_bits_2_25_dataout), .in25(registrador_32_bits_2_26_dataout),
    .in26(registrador_32_bits_2_27_dataout), .in27(registrador_32_bits_2_28_dataout),
    .in28(registrador_32_bits_2_29_dataout), .in29(registrador_32_bits_2_30_dataout),
    .in30(registrador_32_bits_2_31_dataout), .in31(registrador_32_bits_2_32_dataout), .out(\Saída1 ),
    .sel(Registro2));
  Multiplexer #(.select(5), .width(32), .enable("false")) multiplexer_2 (
    .in0(registrador_32_bits_2_1_dataout), .in1(registrador_32_bits_2_2_dataout),
    .in2(registrador_32_bits_2_3_dataout), .in3(registrador_32_bits_2_4_dataout),
    .in4(registrador_32_bits_2_5_dataout), .in5(registrador_32_bits_2_6_dataout),
    .in6(registrador_32_bits_2_7_dataout), .in7(registrador_32_bits_2_8_dataout),
    .in8(registrador_32_bits_2_9_dataout), .in9(registrador_32_bits_2_10_dataout),
    .in10(registrador_32_bits_2_11_dataout), .in11(registrador_32_bits_2_12_dataout),
    .in12(registrador_32_bits_2_13_dataout), .in13(registrador_32_bits_2_14_dataout),
    .in14(registrador_32_bits_2_15_dataout), .in15(registrador_32_bits_2_16_dataout),
    .in16(registrador_32_bits_2_17_dataout), .in17(registrador_32_bits_2_18_dataout),
    .in18(registrador_32_bits_2_19_dataout), .in19(registrador_32_bits_2_20_dataout),
    .in20(registrador_32_bits_2_21_dataout), .in21(registrador_32_bits_2_22_dataout),
    .in22(registrador_32_bits_2_23_dataout), .in23(registrador_32_bits_2_24_dataout),
    .in24(registrador_32_bits_2_25_dataout), .in25(registrador_32_bits_2_26_dataout),
    .in26(registrador_32_bits_2_27_dataout), .in27(registrador_32_bits_2_28_dataout),
    .in28(registrador_32_bits_2_29_dataout), .in29(registrador_32_bits_2_30_dataout),
    .in30(registrador_32_bits_2_31_dataout), .in31(registrador_32_bits_2_32_dataout), .out(\Saída2 ),
    .sel(Registro1));
endmodule

module ULA___FINAL (
  input  in_1,
  input  A,
  input  B,
  input  [4:0] \Opção ,
  output Resultado,
  output Vai1
);

  wire adder_1_out, and_1_out, detector_slt_1_out_2, nor_1_out, or_1_out, subtractor_1_bout,
       subtractor_1_out, xor_1_out;

  and and_1 (and_1_out, A, B);
  or or_1 (or_1_out, A, B);
  xor xor_1 (xor_1_out, A, B);
  nor nor_1 (nor_1_out, A, B);
  Adder #(.width(1)) adder_1 (.a(A), .b(B), .out(adder_1_out), .cin(in_1), .cout(Vai1));
  Subtractor #(.width(1)) subtractor_1 (.a(B), .b(B), .out(subtractor_1_out), .bin(Vai1), .bout(subtractor_1_bout));
  or or_2 (subtractor_1_bout, subtractor_1_out, detector_slt_1_out_2);
  Detector__SLT detector_slt_1 (.in_1(\Opção ), .out_2(detector_slt_1_out_2));
  Multiplexer #(.select(5), .enable("false")) multiplexer_1 (
    .in0(and_1_out), .in1(or_1_out), .in2(xor_1_out), .in3(nor_1_out), .in4(adder_1_out),
    .in5(subtractor_1_out), .in7(B), .in10(B), .in11(B), .in12(B), .in14(B), .out(Resultado), .sel(\Opção ));  // open: in6, in8, in9, in13, in15, in16, in17, in18, in19, in20, in21, in22, in23, in24, in25, in26, in27, in28, in29, in30, in31

  // Notes on the sheet:
  //   OR - 1
  //   XOR - 10
  //   NOR - 11
  //   SOMADOR - 100
  //   SUBTRATOR - 101
  //   Deslocamento Direita - 111
  //   AND - 0
endmodule

module Detector_SLL (
  input  [31:0] Entrada_B,
  input  [4:0] Deslocamento,
  input  [4:0] \Opção ,
  output [31:0] out_4
);

  wire and_1_out;
  wire [4:0] multiplexer_1_out;

  SLL_32 sll_32_1 (.Entrada(Entrada_B), .Deslocamento(multiplexer_1_out), .Deslocados(out_4));
  Multiplexer #(.width(5), .enable("false")) multiplexer_1 (
    .in0({5{1'b0}}), .in1(Deslocamento), .out(multiplexer_1_out), .sel(and_1_out));
  and and_1 (and_1_out, ~\Opção [4], ~\Opção [3], \Opção [2], \Opção [1], \Opção [0]);  // AND_Gate
endmodule

module Detector_SRL (
  input  [31:0] Entrada_B,
  input  [4:0] Deslocamento,
  input  [4:0] \Opção ,
  output [31:0] out_4
);

  wire and_1_out;
  wire [4:0] multiplexer_1_out;

  SLR_32 slr_32_1 (.Entrada(Entrada_B), .Deslocamento(multiplexer_1_out), .Deslocados(out_4));
  Multiplexer #(.width(5), .enable("false")) multiplexer_1 (
    .in0({5{1'b0}}), .in1(Deslocamento), .out(multiplexer_1_out), .sel(and_1_out));
  and and_1 (and_1_out, ~\Opção [4], \Opção [3], \Opção [2], ~\Opção [1], ~\Opção [0]);  // AND_Gate
endmodule

module Detector_SRA (
  input  [31:0] Entrada_B,
  input  [4:0] Deslocamento,
  input  [4:0] \Opção ,
  output [31:0] out_4
);

  wire and_1_out;
  wire [4:0] multiplexer_1_out;

  SRA_32 sra_32_1 (.Entrada(Entrada_B), .Deslocamento(multiplexer_1_out), .Deslocados(out_4));
  Multiplexer #(.width(5), .enable("false")) multiplexer_1 (
    .in0({5{1'b0}}), .in1(Deslocamento), .out(multiplexer_1_out), .sel(and_1_out));
  and and_1 (and_1_out, ~\Opção [4], \Opção [3], \Opção [2], \Opção [1], ~\Opção [0]);  // AND_Gate
endmodule

module Detectores_Aritmeticos (
  input  [31:0] Entrada,
  input  [1:0] in_2,
  input  [4:0] Deslocamento,
  input  [4:0] \Opção ,
  output [31:0] Deslocados
);

  wire [31:0] detector_sll_1_out_4, detector_sra_1_out_4, detector_srl_1_out_4;

  Detector_SLL detector_sll_1 (
    .Entrada_B(Entrada), .Deslocamento(Deslocamento), .\Opção (\Opção ), .out_4(detector_sll_1_out_4));
  Detector_SRL detector_srl_1 (
    .Entrada_B(Entrada), .Deslocamento(Deslocamento), .\Opção (\Opção ), .out_4(detector_srl_1_out_4));
  Detector_SRA detector_sra_1 (
    .Entrada_B(Entrada), .Deslocamento(Deslocamento), .\Opção (\Opção ), .out_4(detector_sra_1_out_4));
  Multiplexer #(.select(2), .width(32), .enable("false")) multiplexer_1 (
    .in0(Entrada), .in1(detector_sll_1_out_4), .in2(detector_srl_1_out_4), .in3(detector_sra_1_out_4),
    .out(Deslocados), .sel(in_2));

  // Notes on the sheet:
  //   SLL - 00111
  //   SRL - 01100
  //   SRA - 01110
endmodule

module SLL (
  input  [31:0] in_1,
  output [31:0] out_2
);


  assign out_2 = {in_1[30:0], 1'b0};
endmodule

module SLL_32 (
  input  [31:0] Entrada,
  input  [4:0] Deslocamento,
  output [31:0] Deslocados
);

  wire [31:0] sll_1_out_2, sll_2_out_2, sll_3_out_2, sll_4_out_2, sll_5_out_2, sll_6_out_2, sll_7_out_2,
       sll_8_out_2, sll_9_out_2, sll_10_out_2, sll_11_out_2, sll_12_out_2, sll_13_out_2, sll_14_out_2,
       sll_15_out_2, sll_16_out_2, sll_17_out_2, sll_18_out_2, sll_19_out_2, sll_20_out_2, sll_21_out_2,
       sll_22_out_2, sll_23_out_2, sll_24_out_2, sll_25_out_2, sll_26_out_2, sll_27_out_2, sll_28_out_2,
       sll_29_out_2, sll_30_out_2, sll_31_out_2;

  SLL sll_1 (.in_1(Entrada), .out_2(sll_1_out_2));
  SLL sll_2 (.in_1(sll_1_out_2), .out_2(sll_2_out_2));
  SLL sll_3 (.in_1(sll_2_out_2), .out_2(sll_3_out_2));
  SLL sll_4 (.in_1(sll_3_out_2), .out_2(sll_4_out_2));
  SLL sll_5 (.in_1(sll_4_out_2), .out_2(sll_5_out_2));
  SLL sll_6 (.in_1(sll_5_out_2), .out_2(sll_6_out_2));
  SLL sll_7 (.in_1(sll_6_out_2), .out_2(sll_7_out_2));
  SLL sll_8 (.in_1(sll_7_out_2), .out_2(sll_8_out_2));
  SLL sll_9 (.in_1(sll_8_out_2), .out_2(sll_9_out_2));
  SLL sll_10 (.in_1(sll_9_out_2), .out_2(sll_10_out_2));
  SLL sll_11 (.in_1(sll_10_out_2), .out_2(sll_11_out_2));
  SLL sll_12 (.in_1(sll_11_out_2), .out_2(sll_12_out_2));
  SLL sll_13 (.in_1(sll_12_out_2), .out_2(sll_13_out_2));
  SLL sll_14 (.in_1(sll_13_out_2), .out_2(sll_14_out_2));
  SLL sll_15 (.in_1(sll_14_out_2), .out_2(sll_15_out_2));
  SLL sll_16 (.in_1(sll_15_out_2), .out_2(sll_16_out_2));
  SLL sll_17 (.in_1(sll_16_out_2), .out_2(sll_17_out_2));
  SLL sll_18 (.in_1(sll_17_out_2), .out_2(sll_18_out_2));
  SLL sll_19 (.in_1(sll_18_out_2), .out_2(sll_19_out_2));
  SLL sll_20 (.in_1(sll_19_out_2), .out_2(sll_20_out_2));
  SLL sll_21 (.in_1(sll_20_out_2), .out_2(sll_21_out_2));
  SLL sll_22 (.in_1(sll_21_out_2), .out_2(sll_22_out_2));
  SLL sll_23 (.in_1(sll_22_out_2), .out_2(sll_23_out_2));
  SLL sll_24 (.in_1(sll_23_out_2), .out_2(sll_24_out_2));
  SLL sll_25 (.in_1(sll_24_out_2), .out_2(sll_25_out_2));
  SLL sll_26 (.in_1(sll_25_out_2), .out_2(sll_26_out_2));
  SLL sll_27 (.in_1(sll_26_out_2), .out_2(sll_27_out_2));
  SLL sll_28 (.in_1(sll_27_out_2), .out_2(sll_28_out_2));
  SLL sll_29 (.in_1(sll_28_out_2), .out_2(sll_29_out_2));
  SLL sll_30 (.in_1(sll_29_out_2), .out_2(sll_30_out_2));
  SLL sll_31 (.in_1(sll_30_out_2), .out_2(sll_31_out_2));
  SLL sll_32 (.in_1(sll_31_out_2));  // open: out_2
  Multiplexer #(.select(5), .width(32), .enable("false")) multiplexer_1 (
    .in0(Entrada), .in1(sll_1_out_2), .in2(sll_2_out_2), .in3(sll_3_out_2), .in4(sll_4_out_2),
    .in5(sll_5_out_2), .in6(sll_6_out_2), .in7(sll_7_out_2), .in8(sll_8_out_2), .in9(sll_9_out_2),
    .in10(sll_10_out_2), .in11(sll_11_out_2), .in12(sll_12_out_2), .in13(sll_13_out_2), .in14(sll_14_out_2),
    .in15(sll_15_out_2), .in16(sll_16_out_2), .in17(sll_17_out_2), .in18(sll_18_out_2), .in19(sll_19_out_2),
    .in20(sll_20_out_2), .in21(sll_21_out_2), .in22(sll_22_out_2), .in23(sll_23_out_2), .in24(sll_24_out_2),
    .in25(sll_25_out_2), .in26(sll_26_out_2), .in27(sll_27_out_2), .in28(sll_28_out_2), .in29(sll_29_out_2),
    .in30(sll_30_out_2), .in31(sll_31_out_2), .out(Deslocados), .sel(Deslocamento));
endmodule

module SLR (
  input  [31:0] in_1,
  output [31:0] out_2
);


  assign out_2 = {1'b0, in_1[31:1]};
endmodule

module SLR_32 (
  input  [31:0] Entrada,
  input  [4:0] Deslocamento,
  output [31:0] Deslocados
);

  wire [31:0] slr_1_out_2, slr_2_out_2, slr_3_out_2, slr_4_out_2, slr_5_out_2, slr_6_out_2, slr_7_out_2,
       slr_8_out_2, slr_9_out_2, slr_10_out_2, slr_11_out_2, slr_12_out_2, slr_13_out_2, slr_14_out_2,
       slr_15_out_2, slr_16_out_2, slr_17_out_2, slr_18_out_2, slr_19_out_2, slr_20_out_2, slr_21_out_2,
       slr_22_out_2, slr_23_out_2, slr_24_out_2, slr_25_out_2, slr_26_out_2, slr_27_out_2, slr_28_out_2,
       slr_29_out_2, slr_30_out_2, slr_31_out_2;

  SLR slr_1 (.in_1(Entrada), .out_2(slr_1_out_2));
  SLR slr_2 (.in_1(slr_1_out_2), .out_2(slr_2_out_2));
  SLR slr_3 (.in_1(slr_2_out_2), .out_2(slr_3_out_2));
  SLR slr_4 (.in_1(slr_3_out_2), .out_2(slr_4_out_2));
  SLR slr_5 (.in_1(slr_4_out_2), .out_2(slr_5_out_2));
  SLR slr_6 (.in_1(slr_5_out_2), .out_2(slr_6_out_2));
  SLR slr_7 (.in_1(slr_6_out_2), .out_2(slr_7_out_2));
  SLR slr_8 (.in_1(slr_7_out_2), .out_2(slr_8_out_2));
  SLR slr_9 (.in_1(slr_8_out_2), .out_2(slr_9_out_2));
  SLR slr_10 (.in_1(slr_9_out_2), .out_2(slr_10_out_2));
  SLR slr_11 (.in_1(slr_10_out_2), .out_2(slr_11_out_2));
  SLR slr_12 (.in_1(slr_11_out_2), .out_2(slr_12_out_2));
  SLR slr_13 (.in_1(slr_12_out_2), .out_2(slr_13_out_2));
  SLR slr_14 (.in_1(slr_13_out_2), .out_2(slr_14_out_2));
  SLR slr_15 (.in_1(slr_14_out_2), .out_2(slr_15_out_2));
  SLR slr_16 (.in_1(slr_15_out_2), .out_2(slr_16_out_2));
  SLR slr_17 (.in_1(slr_16_out_2), .out_2(slr_17_out_2));
  SLR slr_18 (.in_1(slr_17_out_2), .out_2(slr_18_out_2));
  SLR slr_19 (.in_1(slr_18_out_2), .out_2(slr_19_out_2));
  SLR slr_20 (.in_1(slr_19_out_2), .out_2(slr_20_out_2));
  SLR slr_21 (.in_1(slr_20_out_2), .out_2(slr_21_out_2));
  SLR slr_22 (.in_1(slr_21_out_2), .out_2(slr_22_out_2));
  SLR slr_23 (.in_1(slr_22_out_2), .out_2(slr_23_out_2));
  SLR slr_24 (.in_1(slr_23_out_2), .out_2(slr_24_out_2));
  SLR slr_25 (.in_1(slr_24_out_2), .out_2(slr_25_out_2));
  SLR slr_26 (.in_1(slr_25_out_2), .out_2(slr_26_out_2));
  SLR slr_27 (.in_1(slr_26_out_2), .out_2(slr_27_out_2));
  SLR slr_28 (.in_1(slr_27_out_2), .out_2(slr_28_out_2));
  SLR slr_29 (.in_1(slr_28_out_2), .out_2(slr_29_out_2));
  SLR slr_30 (.in_1(slr_29_out_2), .out_2(slr_30_out_2));
  SLR slr_31 (.in_1(slr_30_out_2), .out_2(slr_31_out_2));
  SLR slr_32 (.in_1(slr_31_out_2));  // open: out_2
  Multiplexer #(.select(5), .width(32), .enable("false")) multiplexer_1 (
    .in0(Entrada), .in1(slr_1_out_2), .in2(slr_2_out_2), .in3(slr_3_out_2), .in4(slr_4_out_2),
    .in5(slr_5_out_2), .in6(slr_6_out_2), .in7(slr_7_out_2), .in8(slr_8_out_2), .in9(slr_9_out_2),
    .in10(slr_10_out_2), .in11(slr_11_out_2), .in12(slr_12_out_2), .in13(slr_13_out_2), .in14(slr_14_out_2),
    .in15(slr_15_out_2), .in16(slr_16_out_2), .in17(slr_17_out_2), .in18(slr_18_out_2), .in19(slr_19_out_2),
    .in20(slr_20_out_2), .in21(slr_21_out_2), .in22(slr_22_out_2), .in23(slr_23_out_2), .in24(slr_24_out_2),
    .in25(slr_25_out_2), .in26(slr_26_out_2), .in27(slr_27_out_2), .in28(slr_28_out_2), .in29(slr_29_out_2),
    .in30(slr_30_out_2), .in31(slr_31_out_2), .out(Deslocados), .sel(Deslocamento));
endmodule

module SRA (
  input  [31:0] in_1,
  output [31:0] out_2
);


  assign out_2 = {{2{in_1[31]}}, in_1[30:1]};
endmodule

module SRA_32 (
  input  [31:0] Entrada,
  input  [4:0] Deslocamento,
  output [31:0] Deslocados
);

  wire [31:0] sra_1_out_2, sra_2_out_2, sra_3_out_2, sra_4_out_2, sra_5_out_2, sra_6_out_2, sra_7_out_2,
       sra_8_out_2, sra_9_out_2, sra_10_out_2, sra_11_out_2, sra_12_out_2, sra_13_out_2, sra_14_out_2,
       sra_15_out_2, sra_16_out_2, sra_17_out_2, sra_18_out_2, sra_19_out_2, sra_20_out_2, sra_21_out_2,
       sra_22_out_2, sra_23_out_2, sra_24_out_2, sra_25_out_2, sra_26_out_2, sra_27_out_2, sra_28_out_2,
       sra_29_out_2, sra_30_out_2, sra_31_out_2;

  SRA sra_1 (.in_1(Entrada), .out_2(sra_1_out_2));
  SRA sra_2 (.in_1(sra_1_out_2), .out_2(sra_2_out_2));
  SRA sra_3 (.in_1(sra_2_out_2), .out_2(sra_3_out_2));
  SRA sra_4 (.in_1(sra_3_out_2), .out_2(sra_4_out_2));
  SRA sra_5 (.in_1(sra_4_out_2), .out_2(sra_5_out_2));
  SRA sra_6 (.in_1(sra_5_out_2), .out_2(sra_6_out_2));
  SRA sra_7 (.in_1(sra_6_out_2), .out_2(sra_7_out_2));
  SRA sra_8 (.in_1(sra_7_out_2), .out_2(sra_8_out_2));
  SRA sra_9 (.in_1(sra_8_out_2), .out_2(sra_9_out_2));
  SRA sra_10 (.in_1(sra_9_out_2), .out_2(sra_10_out_2));
  SRA sra_11 (.in_1(sra_10_out_2), .out_2(sra_11_out_2));
  SRA sra_12 (.in_1(sra_11_out_2), .out_2(sra_12_out_2));
  SRA sra_13 (.in_1(sra_12_out_2), .out_2(sra_13_out_2));
  SRA sra_14 (.in_1(sra_13_out_2), .out_2(sra_14_out_2));
  SRA sra_15 (.in_1(sra_14_out_2), .out_2(sra_15_out_2));
  SRA sra_16 (.in_1(sra_15_out_2), .out_2(sra_16_out_2));
  SRA sra_17 (.in_1(sra_16_out_2), .out_2(sra_17_out_2));
  SRA sra_18 (.in_1(sra_17_out_2), .out_2(sra_18_out_2));
  SRA sra_19 (.in_1(sra_18_out_2), .out_2(sra_19_out_2));
  SRA sra_20 (.in_1(sra_19_out_2), .out_2(sra_20_out_2));
  SRA sra_21 (.in_1(sra_20_out_2), .out_2(sra_21_out_2));
  SRA sra_22 (.in_1(sra_21_out_2), .out_2(sra_22_out_2));
  SRA sra_23 (.in_1(sra_22_out_2), .out_2(sra_23_out_2));
  SRA sra_24 (.in_1(sra_23_out_2), .out_2(sra_24_out_2));
  SRA sra_25 (.in_1(sra_24_out_2), .out_2(sra_25_out_2));
  SRA sra_26 (.in_1(sra_25_out_2), .out_2(sra_26_out_2));
  SRA sra_27 (.in_1(sra_26_out_2), .out_2(sra_27_out_2));
  SRA sra_28 (.in_1(sra_27_out_2), .out_2(sra_28_out_2));
  SRA sra_29 (.in_1(sra_28_out_2), .out_2(sra_29_out_2));
  SRA sra_30 (.in_1(sra_29_out_2), .out_2(sra_30_out_2));
  SRA sra_31 (.in_1(sra_30_out_2), .out_2(sra_31_out_2));
  SRA sra_32 (.in_1(sra_31_out_2));  // open: out_2
  Multiplexer #(.select(5), .width(32), .enable("false")) multiplexer_1 (
    .in0(Entrada), .in1(sra_1_out_2), .in2(sra_2_out_2), .in3(sra_3_out_2), .in4(sra_4_out_2),
    .in5(sra_5_out_2), .in6(sra_6_out_2), .in7(sra_7_out_2), .in8(sra_8_out_2), .in9(sra_9_out_2),
    .in10(sra_10_out_2), .in11(sra_11_out_2), .in12(sra_12_out_2), .in13(sra_13_out_2), .in14(sra_14_out_2),
    .in15(sra_15_out_2), .in16(sra_16_out_2), .in17(sra_17_out_2), .in18(sra_18_out_2), .in19(sra_19_out_2),
    .in20(sra_20_out_2), .in21(sra_21_out_2), .in22(sra_22_out_2), .in23(sra_23_out_2), .in24(sra_24_out_2),
    .in25(sra_25_out_2), .in26(sra_26_out_2), .in27(sra_27_out_2), .in28(sra_28_out_2), .in29(sra_29_out_2),
    .in30(sra_30_out_2), .in31(sra_31_out_2), .out(Deslocados), .sel(Deslocamento));
endmodule

module ULA_32___FINAL (
  input  [31:0] A,
  input  [31:0] B,
  input  [1:0] Deslocados,
  input  [4:0] Deslocamento,
  input  [4:0] \Opção ,
  output out_6,
  output OverFlowNat,
  output [31:0] Resultado
);

  wire detector_slt_1_out_2, \detector_subtração_1_sub , multiplexer_2_out, or_1_out, ula_final_2_vai1,
       ula_final_3_vai1, ula_final_4_vai1, ula_final_5_vai1, ula_final_6_vai1, ula_final_7_vai1,
       ula_final_8_vai1, ula_final_9_vai1, ula_final_10_vai1, ula_final_11_vai1, ula_final_12_vai1,
       ula_final_13_vai1, ula_final_14_vai1, ula_final_15_vai1, ula_final_16_vai1, ula_final_17_vai1,
       ula_final_18_vai1, ula_final_19_vai1, ula_final_20_vai1, ula_final_21_vai1, ula_final_22_vai1,
       ula_final_23_vai1, ula_final_24_vai1, ula_final_25_vai1, ula_final_26_vai1, ula_final_27_vai1,
       ula_final_28_vai1, ula_final_29_vai1, ula_final_30_vai1, ula_final_31_vai1, ula_final_32_vai1;
  wire [31:0] detectores_aritmeticos_1_deslocados, ula_final_32_resultado;

  Detectores_Aritmeticos detectores_aritmeticos_1 (
    .Entrada(B), .Deslocamento(Deslocamento), .\Opção (\Opção ), .in_2(Deslocados),
    .Deslocados(detectores_aritmeticos_1_deslocados));
  OverFlowInt overflowint_1 (
    .in_1(ula_final_32_resultado[31]), .in_2(detectores_aritmeticos_1_deslocados[31]), .in_3(A[31]),
    .out_4(out_6));
  ULA___FINAL ula_final_1 (
    .Vai1(OverFlowNat), .A(A[31]), .B(detectores_aritmeticos_1_deslocados[31]), .\Opção (\Opção ),
    .in_1(ula_final_2_vai1), .Resultado(ula_final_32_resultado[31]));
  ULA___FINAL ula_final_2 (
    .Vai1(ula_final_2_vai1), .A(A[30]), .B(detectores_aritmeticos_1_deslocados[30]), .\Opção (\Opção ),
    .in_1(ula_final_4_vai1), .Resultado(ula_final_32_resultado[30]));
  ULA___FINAL ula_final_3 (
    .Vai1(ula_final_3_vai1), .A(A[28]), .B(detectores_aritmeticos_1_deslocados[28]), .\Opção (\Opção ),
    .in_1(ula_final_5_vai1), .Resultado(ula_final_32_resultado[28]));
  ULA___FINAL ula_final_4 (
    .Vai1(ula_final_4_vai1), .A(A[29]), .B(detectores_aritmeticos_1_deslocados[29]), .\Opção (\Opção ),
    .in_1(ula_final_3_vai1), .Resultado(ula_final_32_resultado[29]));
  ULA___FINAL ula_final_5 (
    .Vai1(ula_final_5_vai1), .A(A[27]), .B(detectores_aritmeticos_1_deslocados[27]), .\Opção (\Opção ),
    .in_1(ula_final_6_vai1), .Resultado(ula_final_32_resultado[27]));
  ULA___FINAL ula_final_6 (
    .Vai1(ula_final_6_vai1), .A(A[26]), .B(detectores_aritmeticos_1_deslocados[26]), .\Opção (\Opção ),
    .in_1(ula_final_7_vai1), .Resultado(ula_final_32_resultado[26]));
  ULA___FINAL ula_final_7 (
    .Vai1(ula_final_7_vai1), .A(A[25]), .B(detectores_aritmeticos_1_deslocados[25]), .\Opção (\Opção ),
    .in_1(ula_final_8_vai1), .Resultado(ula_final_32_resultado[25]));
  ULA___FINAL ula_final_8 (
    .Vai1(ula_final_8_vai1), .A(A[24]), .B(detectores_aritmeticos_1_deslocados[24]), .\Opção (\Opção ),
    .in_1(ula_final_9_vai1), .Resultado(ula_final_32_resultado[24]));
  ULA___FINAL ula_final_9 (
    .Vai1(ula_final_9_vai1), .A(A[23]), .B(detectores_aritmeticos_1_deslocados[23]), .\Opção (\Opção ),
    .in_1(ula_final_10_vai1), .Resultado(ula_final_32_resultado[23]));
  ULA___FINAL ula_final_10 (
    .Vai1(ula_final_10_vai1), .A(A[22]), .B(detectores_aritmeticos_1_deslocados[22]), .\Opção (\Opção ),
    .in_1(ula_final_12_vai1), .Resultado(ula_final_32_resultado[22]));
  ULA___FINAL ula_final_11 (
    .Vai1(ula_final_11_vai1), .A(A[20]), .B(detectores_aritmeticos_1_deslocados[20]), .\Opção (\Opção ),
    .in_1(ula_final_13_vai1), .Resultado(ula_final_32_resultado[20]));
  ULA___FINAL ula_final_12 (
    .Vai1(ula_final_12_vai1), .A(A[21]), .B(detectores_aritmeticos_1_deslocados[21]), .\Opção (\Opção ),
    .in_1(ula_final_11_vai1), .Resultado(ula_final_32_resultado[21]));
  ULA___FINAL ula_final_13 (
    .Vai1(ula_final_13_vai1), .A(A[19]), .B(detectores_aritmeticos_1_deslocados[19]), .\Opção (\Opção ),
    .in_1(ula_final_14_vai1), .Resultado(ula_final_32_resultado[19]));
  ULA___FINAL ula_final_14 (
    .Vai1(ula_final_14_vai1), .A(A[18]), .B(detectores_aritmeticos_1_deslocados[18]), .\Opção (\Opção ),
    .in_1(ula_final_16_vai1), .Resultado(ula_final_32_resultado[18]));
  ULA___FINAL ula_final_15 (
    .Vai1(ula_final_15_vai1), .A(A[16]), .B(detectores_aritmeticos_1_deslocados[16]), .\Opção (\Opção ),
    .in_1(ula_final_17_vai1), .Resultado(ula_final_32_resultado[16]));
  ULA___FINAL ula_final_16 (
    .Vai1(ula_final_16_vai1), .A(A[17]), .B(detectores_aritmeticos_1_deslocados[17]), .\Opção (\Opção ),
    .in_1(ula_final_15_vai1), .Resultado(ula_final_32_resultado[17]));
  ULA___FINAL ula_final_17 (
    .Vai1(ula_final_17_vai1), .A(A[15]), .B(detectores_aritmeticos_1_deslocados[15]), .\Opção (\Opção ),
    .in_1(ula_final_18_vai1), .Resultado(ula_final_32_resultado[15]));
  ULA___FINAL ula_final_18 (
    .Vai1(ula_final_18_vai1), .A(A[14]), .B(detectores_aritmeticos_1_deslocados[14]), .\Opção (\Opção ),
    .in_1(ula_final_20_vai1), .Resultado(ula_final_32_resultado[14]));
  ULA___FINAL ula_final_19 (
    .Vai1(ula_final_19_vai1), .A(A[12]), .B(detectores_aritmeticos_1_deslocados[12]), .\Opção (\Opção ),
    .in_1(ula_final_21_vai1), .Resultado(ula_final_32_resultado[12]));
  ULA___FINAL ula_final_20 (
    .Vai1(ula_final_20_vai1), .A(A[13]), .B(detectores_aritmeticos_1_deslocados[13]), .\Opção (\Opção ),
    .in_1(ula_final_19_vai1), .Resultado(ula_final_32_resultado[13]));
  ULA___FINAL ula_final_21 (
    .Vai1(ula_final_21_vai1), .A(A[11]), .B(detectores_aritmeticos_1_deslocados[11]), .\Opção (\Opção ),
    .in_1(ula_final_22_vai1), .Resultado(ula_final_32_resultado[11]));
  ULA___FINAL ula_final_22 (
    .Vai1(ula_final_22_vai1), .A(A[10]), .B(detectores_aritmeticos_1_deslocados[10]), .\Opção (\Opção ),
    .in_1(ula_final_24_vai1), .Resultado(ula_final_32_resultado[10]));
  ULA___FINAL ula_final_23 (
    .Vai1(ula_final_23_vai1), .A(A[8]), .B(detectores_aritmeticos_1_deslocados[8]), .\Opção (\Opção ),
    .in_1(ula_final_25_vai1), .Resultado(ula_final_32_resultado[8]));
  ULA___FINAL ula_final_24 (
    .Vai1(ula_final_24_vai1), .A(A[9]), .B(detectores_aritmeticos_1_deslocados[9]), .\Opção (\Opção ),
    .in_1(ula_final_23_vai1), .Resultado(ula_final_32_resultado[9]));
  ULA___FINAL ula_final_25 (
    .Vai1(ula_final_25_vai1), .A(A[7]), .B(detectores_aritmeticos_1_deslocados[7]), .\Opção (\Opção ),
    .in_1(ula_final_26_vai1), .Resultado(ula_final_32_resultado[7]));
  ULA___FINAL ula_final_26 (
    .Vai1(ula_final_26_vai1), .A(A[6]), .B(detectores_aritmeticos_1_deslocados[6]), .\Opção (\Opção ),
    .in_1(ula_final_27_vai1), .Resultado(ula_final_32_resultado[6]));
  ULA___FINAL ula_final_27 (
    .Vai1(ula_final_27_vai1), .A(A[5]), .B(detectores_aritmeticos_1_deslocados[5]), .\Opção (\Opção ),
    .in_1(ula_final_28_vai1), .Resultado(ula_final_32_resultado[5]));
  ULA___FINAL ula_final_28 (
    .Vai1(ula_final_28_vai1), .A(A[4]), .B(detectores_aritmeticos_1_deslocados[4]), .\Opção (\Opção ),
    .in_1(ula_final_29_vai1), .Resultado(ula_final_32_resultado[4]));
  ULA___FINAL ula_final_29 (
    .Vai1(ula_final_29_vai1), .A(A[3]), .B(detectores_aritmeticos_1_deslocados[3]), .\Opção (\Opção ),
    .in_1(ula_final_30_vai1), .Resultado(ula_final_32_resultado[3]));
  Multiplexer #(.width(32), .enable("false")) multiplexer_1 (
    .in0(ula_final_32_resultado), .in1({{31{1'b0}}, ula_final_32_resultado[31]}), .out(Resultado),
    .sel(detector_slt_1_out_2));
  \Detector_Subtração  \detector_subtração_1  (.Sub(\detector_subtração_1_sub ), .in_1(\Opção ));
  Detector__SLT detector_slt_1 (.in_1(\Opção ), .out_2(detector_slt_1_out_2));
  ULA___FINAL ula_final_30 (
    .Vai1(ula_final_30_vai1), .A(A[2]), .B(detectores_aritmeticos_1_deslocados[2]), .\Opção (\Opção ),
    .in_1(ula_final_31_vai1), .Resultado(ula_final_32_resultado[2]));
  or or_1 (or_1_out, \detector_subtração_1_sub , detector_slt_1_out_2);
  ULA___FINAL ula_final_31 (
    .Vai1(ula_final_31_vai1), .A(A[1]), .B(detectores_aritmeticos_1_deslocados[1]), .\Opção (\Opção ),
    .in_1(ula_final_32_vai1), .Resultado(ula_final_32_resultado[1]));
  ULA___FINAL ula_final_32 (
    .Vai1(ula_final_32_vai1), .A(A[0]), .B(detectores_aritmeticos_1_deslocados[0]), .\Opção (\Opção ),
    .in_1(multiplexer_2_out), .Resultado(ula_final_32_resultado[0]));
  Multiplexer #(.enable("false")) multiplexer_2 (.in0(1'b1), .in1(1'b0), .out(multiplexer_2_out), .sel(or_1_out));

  // Notes on the sheet:
  //   SLL - 00111
  //   SRL - 01100
  //   SRA - 01110
endmodule

module Banco_Registrador_32___FINAL (
  input  [4:0] Registro2,
  input  LImpar,
  input  Salvar,
  input  [4:0] Destino,
  input  [4:0] Registro1,
  input  [31:0] Entrada,
  output [31:0] \Saída1 ,
  output [31:0] \Saída2 
);

  wire demultiplexer_1_out0, demultiplexer_1_out1, demultiplexer_1_out2, demultiplexer_1_out3,
       demultiplexer_1_out4, demultiplexer_1_out5, demultiplexer_1_out6, demultiplexer_1_out7,
       demultiplexer_1_out8, demultiplexer_1_out9, demultiplexer_1_out10, demultiplexer_1_out11,
       demultiplexer_1_out12, demultiplexer_1_out13, demultiplexer_1_out14, demultiplexer_1_out15,
       demultiplexer_1_out16, demultiplexer_1_out17, demultiplexer_1_out18, demultiplexer_1_out19,
       demultiplexer_1_out20, demultiplexer_1_out21, demultiplexer_1_out22, demultiplexer_1_out23,
       demultiplexer_1_out24, demultiplexer_1_out25, demultiplexer_1_out26, demultiplexer_1_out27,
       demultiplexer_1_out28, demultiplexer_1_out29, demultiplexer_1_out30, demultiplexer_1_out31;
  wire [31:0] register_1_q, register_2_q, register_3_q, register_4_q, register_5_q, register_6_q,
       register_7_q, register_8_q, register_9_q, register_10_q, register_11_q, register_12_q, register_13_q,
       register_14_q, register_15_q, register_16_q, register_17_q, register_18_q, register_19_q,
       register_20_q, register_21_q, register_22_q, register_23_q, register_24_q, register_25_q,
       register_26_q, register_27_q, register_28_q, register_29_q, register_30_q, register_31_q,
       register_32_q;

  Demultiplexer #(.select(5), .enable("false")) demultiplexer_1 (
    .out0(demultiplexer_1_out0), .out1(demultiplexer_1_out1), .out2(demultiplexer_1_out2),
    .out3(demultiplexer_1_out3), .out4(demultiplexer_1_out4), .out5(demultiplexer_1_out5),
    .out6(demultiplexer_1_out6), .out7(demultiplexer_1_out7), .out8(demultiplexer_1_out8),
    .out9(demultiplexer_1_out9), .out10(demultiplexer_1_out10), .out11(demultiplexer_1_out11),
    .out12(demultiplexer_1_out12), .out13(demultiplexer_1_out13), .out14(demultiplexer_1_out14),
    .out15(demultiplexer_1_out15), .out16(demultiplexer_1_out16), .out17(demultiplexer_1_out17),
    .out18(demultiplexer_1_out18), .out19(demultiplexer_1_out19), .out20(demultiplexer_1_out20),
    .out21(demultiplexer_1_out21), .out22(demultiplexer_1_out22), .out23(demultiplexer_1_out23),
    .out24(demultiplexer_1_out24), .out25(demultiplexer_1_out25), .out26(demultiplexer_1_out26),
    .out27(demultiplexer_1_out27), .out28(demultiplexer_1_out28), .out29(demultiplexer_1_out29),
    .out30(demultiplexer_1_out30), .out31(demultiplexer_1_out31), .in(Salvar), .sel(Destino));
  Register #(.width(32)) register_1 (
    .D(Entrada), .Q(register_1_q), .clk(demultiplexer_1_out0), .clr(LImpar));  // open: en
  Register #(.width(32)) register_2 (
    .D(Entrada), .Q(register_2_q), .clk(demultiplexer_1_out1), .clr(LImpar));  // open: en
  Register #(.width(32)) register_3 (
    .D(Entrada), .Q(register_3_q), .clk(demultiplexer_1_out2), .clr(LImpar));  // open: en
  Register #(.width(32)) register_4 (
    .D(Entrada), .Q(register_4_q), .clk(demultiplexer_1_out3), .clr(LImpar));  // open: en
  Register #(.width(32)) register_5 (
    .D(Entrada), .Q(register_5_q), .clk(demultiplexer_1_out4), .clr(LImpar));  // open: en
  Register #(.width(32)) register_6 (
    .D(Entrada), .Q(register_6_q), .clk(demultiplexer_1_out5), .clr(LImpar));  // open: en
  Register #(.width(32)) register_7 (
    .D(Entrada), .Q(register_7_q), .clk(demultiplexer_1_out6), .clr(LImpar));  // open: en
  Register #(.width(32)) register_8 (
    .D(Entrada), .Q(register_8_q), .clk(demultiplexer_1_out7), .clr(LImpar));  // open: en
  Register #(.width(32)) register_9 (
    .D(Entrada), .Q(register_9_q), .clk(demultiplexer_1_out8), .clr(LImpar));  // open: en
  Register #(.width(32)) register_10 (
    .D(Entrada), .Q(register_10_q), .clk(demultiplexer_1_out9), .clr(LImpar));  // open: en
  Register #(.width(32)) register_11 (
    .D(Entrada), .Q(register_11_q), .clk(demultiplexer_1_out10), .clr(LImpar));  // open: en
  Register #(.width(32)) register_12 (
    .D(Entrada), .Q(register_12_q), .clk(demultiplexer_1_out11), .clr(LImpar));  // open: en
  Register #(.width(32)) register_13 (
    .D(Entrada), .Q(register_13_q), .clk(demultiplexer_1_out12), .clr(LImpar));  // open: en
  Register #(.width(32)) register_14 (
    .D(Entrada), .Q(register_14_q), .clk(demultiplexer_1_out13), .clr(LImpar));  // open: en
  Register #(.width(32)) register_15 (
    .D(Entrada), .Q(register_15_q), .clk(demultiplexer_1_out14), .clr(LImpar));  // open: en
  Register #(.width(32)) register_16 (
    .D(Entrada), .Q(register_16_q), .clk(demultiplexer_1_out15), .clr(LImpar));  // open: en
  Register #(.width(32)) register_17 (
    .D(Entrada), .Q(register_17_q), .clk(demultiplexer_1_out16), .clr(LImpar));  // open: en
  Register #(.width(32)) register_18 (
    .D(Entrada), .Q(register_18_q), .clk(demultiplexer_1_out17), .clr(LImpar));  // open: en
  Register #(.width(32)) register_19 (
    .D(Entrada), .Q(register_19_q), .clk(demultiplexer_1_out18), .clr(LImpar));  // open: en
  Register #(.width(32)) register_20 (
    .D(Entrada), .Q(register_20_q), .clk(demultiplexer_1_out19), .clr(LImpar));  // open: en
  Register #(.width(32)) register_21 (
    .D(Entrada), .Q(register_21_q), .clk(demultiplexer_1_out20), .clr(LImpar));  // open: en
  Register #(.width(32)) register_22 (
    .D(Entrada), .Q(register_22_q), .clk(demultiplexer_1_out21), .clr(LImpar));  // open: en
  Register #(.width(32)) register_23 (
    .D(Entrada), .Q(register_23_q), .clk(demultiplexer_1_out22), .clr(LImpar));  // open: en
  Register #(.width(32)) register_24 (
    .D(Entrada), .Q(register_24_q), .clk(demultiplexer_1_out23), .clr(LImpar));  // open: en
  Register #(.width(32)) register_25 (
    .D(Entrada), .Q(register_25_q), .clk(demultiplexer_1_out24), .clr(LImpar));  // open: en
  Register #(.width(32)) register_26 (
    .D(Entrada), .Q(register_26_q), .clk(demultiplexer_1_out25), .clr(LImpar));  // open: en
  Register #(.width(32)) register_27 (
    .D(Entrada), .Q(register_27_q), .clk(demultiplexer_1_out26), .clr(LImpar));  // open: en
  Register #(.width(32)) register_28 (
    .D(Entrada), .Q(register_28_q), .clk(demultiplexer_1_out27), .clr(LImpar));  // open: en
  Register #(.width(32)) register_29 (
    .D(Entrada), .Q(register_29_q), .clk(demultiplexer_1_out28), .clr(LImpar));  // open: en
  Register #(.width(32)) register_30 (
    .D(Entrada), .Q(register_30_q), .clk(demultiplexer_1_out29), .clr(LImpar));  // open: en
  Register #(.width(32)) register_31 (
    .D(Entrada), .Q(register_31_q), .clk(demultiplexer_1_out30), .clr(LImpar));  // open: en
  Register #(.width(32)) register_32 (
    .D(Entrada), .Q(register_32_q), .clk(demultiplexer_1_out31), .clr(LImpar));  // open: en
  Multiplexer #(.select(5), .width(32), .enable("false")) multiplexer_1 (
    .in0(register_1_q), .in1(register_2_q), .in2(register_3_q), .in3(register_4_q), .in4(register_5_q),
    .in5(register_6_q), .in6(register_7_q), .in7(register_8_q), .in8(register_9_q), .in9(register_10_q),
    .in10(register_11_q), .in11(register_12_q), .in12(register_13_q), .in13(register_14_q),
    .in14(register_15_q), .in15(register_16_q), .in16(register_17_q), .in17(register_18_q),
    .in18(register_19_q), .in19(register_20_q), .in20(register_21_q), .in21(register_22_q),
    .in22(register_23_q), .in23(register_24_q), .in24(register_25_q), .in25(register_26_q),
    .in26(register_27_q), .in27(register_28_q), .in28(register_29_q), .in29(register_30_q),
    .in30(register_31_q), .in31(register_32_q), .out(\Saída1 ), .sel(Registro2));
  Multiplexer #(.select(5), .width(32), .enable("false")) multiplexer_2 (
    .in0(register_1_q), .in1(register_2_q), .in2(register_3_q), .in3(register_4_q), .in4(register_5_q),
    .in5(register_6_q), .in6(register_7_q), .in7(register_8_q), .in8(register_9_q), .in9(register_10_q),
    .in10(register_11_q), .in11(register_12_q), .in12(register_13_q), .in13(register_14_q),
    .in14(register_15_q), .in15(register_16_q), .in16(register_17_q), .in17(register_18_q),
    .in18(register_19_q), .in19(register_20_q), .in20(register_21_q), .in21(register_22_q),
    .in22(register_23_q), .in23(register_24_q), .in24(register_25_q), .in25(register_26_q),
    .in26(register_27_q), .in27(register_28_q), .in28(register_29_q), .in29(register_30_q),
    .in30(register_31_q), .in31(register_32_q), .out(\Saída2 ), .sel(Registro1));
endmodule

module \Junção_ULA___BR  (
  input  [4:0] Deslocamento,
  input  CLK,
  input  RESET,
  input  [1:0] Deslocador,
  input  [4:0] RT,
  input  [4:0] RD,
  input  [4:0] RS,
  input  i,
  input  [4:0] \Opção ,
  input  [31:0] IMM,
  output OverFlowNat
);

  wire [31:0] \banco_registrador_32_final_1_saída1 , \banco_registrador_32_final_1_saída2 ,
       multiplexer_1_out, ula_32_final_1_resultado;

  Multiplexer #(.width(32), .enable("false")) multiplexer_1 (
    .in0(\banco_registrador_32_final_1_saída2 ), .in1(IMM), .out(multiplexer_1_out), .sel(i));
  ULA_32___FINAL ula_32_final_1 (
    .A(\banco_registrador_32_final_1_saída1 ), .B(multiplexer_1_out), .\Opção (\Opção ),
    .OverFlowNat(OverFlowNat), .Resultado(ula_32_final_1_resultado), .Deslocamento(Deslocamento),
    .Deslocados(Deslocador));  // open: out_6
  Banco_Registrador_32___FINAL banco_registrador_32_final_1 (
    .Registro2(RT), .LImpar(RESET), .Salvar(CLK), .Entrada(ula_32_final_1_resultado), .Destino(RD),
    .Registro1(RS), .\Saída1 (\banco_registrador_32_final_1_saída1 ),
    .\Saída2 (\banco_registrador_32_final_1_saída2 ));

  // Notes on the sheet:
  //   SLL - 00111
  //   SRL - 01100
  //   SRA - 01110
  //   SOMADOR - 100
endmodule
